// Logisim project Forward A & B.circ as structural Verilog: 1 circuit, main circuit main
module main (
  input  [4:0] Rs1_EX,
  input  MemRead_MEM,
  input  RegWrite_MEM,
  input  RegWrite_WB,
  input  [4:0] Reg_Des_WB,
  input  [4:0] Rs2_EX,
  input  [4:0] Reg_Des_MEM,
  output [1:0] Forward_A,
  output [1:0] Forward_B
);

  wire and_1_out, and_2_out, and_3_out, and_4_out, and_5_out, and_6_out, comparator_1_eq, comparator_2_eq,
       comparator_3_eq, comparator_4_eq, comparator_5_eq, comparator_6_eq, comparator_7_eq, comparator_8_eq,
       Rs1_not_Zero, Rs2_not_Zero;

  Comparator #(.width(5), .mode("unsigned")) comparator_1 (
    .a(Rs1_EX), .b(Reg_Des_MEM), .eq(comparator_1_eq));  // open: gt, lt
  Comparator #(.width(5), .mode("unsigned")) comparator_2 (
    .a(Rs1_EX), .b(Reg_Des_WB), .eq(comparator_2_eq));  // open: gt, lt
  Comparator #(.width(5), .mode("unsigned")) comparator_3 (
    .a(Rs1_EX), .b(Reg_Des_MEM), .eq(comparator_3_eq));  // open: gt, lt
  and and_1 (and_1_out, RegWrite_MEM, comparator_1_eq, Rs1_not_Zero);
  and and_2 (and_2_out, ~and_1_out, RegWrite_WB, comparator_2_eq, Rs1_not_Zero);  // AND_Gate
  and and_3 (and_3_out, ~and_1_out, ~and_2_out, MemRead_MEM, RegWrite_MEM, comparator_3_eq, Rs1_not_Zero);  // AND_Gate
  or or_1 (Forward_A[0], and_1_out, and_2_out);
  or or_2 (Forward_A[1], and_2_out, and_3_out);
  Comparator #(.width(5), .mode("unsigned")) comparator_4 (
    .a(Rs2_EX), .b(Reg_Des_MEM), .eq(comparator_4_eq));  // open: gt, lt
  Comparator #(.width(5), .mode("unsigned")) comparator_5 (
    .a(Rs2_EX), .b(Reg_Des_WB), .eq(comparator_5_eq));  // open: gt, lt
  Comparator #(.width(5), .mode("unsigned")) comparator_6 (
    .a(Rs2_EX), .b(Reg_Des_MEM), .eq(comparator_6_eq));  // open: gt, lt
  Comparator #(.width(5), .mode("unsigned")) comparator_7 (
    .a(Rs1_EX), .b({5{1'b0}}), .eq(comparator_7_eq));  // open: gt, lt
  Comparator #(.width(5), .mode("unsigned")) comparator_8 (
    .a(Rs2_EX), .b({5{1'b0}}), .eq(comparator_8_eq));  // open: gt, lt
  not not_1 (Rs1_not_Zero, comparator_7_eq);
  not not_2 (Rs2_not_Zero, comparator_8_eq);
  and and_4 (and_4_out, RegWrite_MEM, comparator_4_eq, Rs2_not_Zero);
  and and_5 (and_5_out, ~and_4_out, RegWrite_WB, comparator_5_eq, Rs2_not_Zero);  // AND_Gate
  and and_6 (and_6_out, ~and_4_out, ~and_5_out, MemRead_MEM, RegWrite_MEM, comparator_6_eq, Rs2_not_Zero);  // AND_Gate
  or or_3 (Forward_B[0], and_4_out, and_5_out);
  or or_4 (Forward_B[1], and_5_out, and_6_out);

  // Notes on the sheet:
  //   LW
  //   previous
  //   2nd previos
  //   previous
  //   2nd previos
  //   LW
endmodule
