// Logisim project pc_circut.circ as structural Verilog: 1 circuit, main circuit main
module main (
  input  [10:0] upper11,
  input  [4:0] Lower5,
  input  stall,
  input  in_4,
  input  pc_src,
  input  [19:0] PC_ID,
  input  jalr,
  input  [15:0] IMM16,
  input  [31:0] RS1,
  output [19:0] out_10,
  output [19:0] out_11
);

  wire not_1_out;
  wire [19:0] adder_2_out, adder_3_out, bit_extender_1_out, bit_extender_2_out, multiplexer_1_out,
       multiplexer_2_out;

  // Probe on {upper11, Lower5}
  not not_1 (not_1_out, stall);
  assign bit_extender_1_out = {{4{upper11[10]}}, {upper11, Lower5}};  // Bit_Extender bit_extender_1
  // Probe on out_11
  Register #(.width(20)) register_1 (.D(multiplexer_2_out), .en(not_1_out), .clk(in_4), .Q(out_11));  // open: clr
  assign bit_extender_2_out = {{4{IMM16[15]}}, IMM16};  // Bit_Extender bit_extender_2
  // Probe on out_10
  Adder #(.width(20)) adder_1 (.a(out_11), .b(20'h1), .out(out_10), .cin(1'b0));  // open: cout
  Adder #(.width(20)) adder_2 (.a(bit_extender_1_out), .b(PC_ID), .out(adder_2_out), .cin(1'b0));  // open: cout
  Adder #(.width(20)) adder_3 (.a(bit_extender_2_out), .b(RS1[19:0]), .out(adder_3_out), .cin(1'b0));  // open: cout
  // Probe on multiplexer_2_out
  Multiplexer #(.width(20), .enable("false")) multiplexer_1 (
    .in0(out_10), .in1(adder_2_out), .out(multiplexer_1_out), .sel(pc_src));
  Multiplexer #(.width(20), .enable("false")) multiplexer_2 (
    .in0(multiplexer_1_out), .in1(adder_3_out), .out(multiplexer_2_out), .sel(jalr));

  // Other names for the same wires on the sheet: pc[19:0] = out_11; pc_inc[19:0] = out_10

  // Notes on the sheet:
  //   pc+1
endmodule
