// Logisim project pc_control_unit.circ as structural Verilog: 1 circuit, main circuit main
module main (
  input  BEQ,
  input  zero_flag,
  input  BNE,
  input  BLT,
  input  in_5,
  input  BGE,
  input  BLTU,
  input  in_8,
  input  BGEU,
  input  JALR,
  output Pc_src,
  output jalr_2
);

  wire and_1_out, and_2_out, and_3_out, and_4_out, and_5_out, and_6_out;

  and and_1 (and_1_out, BEQ, zero_flag);
  and and_2 (and_2_out, ~zero_flag, BNE);  // AND_Gate
  and and_3 (and_3_out, BLT, in_5);
  and and_4 (and_4_out, ~in_5, BGE);  // AND_Gate
  and and_5 (and_5_out, BLTU, in_8);
  and and_6 (and_6_out, ~in_8, BGEU);  // AND_Gate
  or or_1 (Pc_src, and_1_out, and_2_out, and_3_out, and_4_out, and_5_out, and_6_out);

  assign jalr_2 = JALR;

  // Notes on the sheet:
  //   less_flag_unsigned
  //   less_flag__signed
endmodule
