// Logisim project ALU.circ as structural Verilog: 3 circuits, main circuit main
module main (
);

  ALU alu_1 ();  // open: Operation, AInvert, BInvert, CarryIn, select_Alu, Branching, in_4, in_2, CarryOut, OverFlow, Alu_Result, branch_output
endmodule

module ALU (
  input  CarryIn,
  input  [31:0] in_2,
  input  [3:0] select_Alu,
  input  [31:0] in_4,
  input  [2:0] Branching,
  input  [1:0] Operation,
  input  AInvert,
  input  BInvert,
  output [31:0] Alu_Result,
  output branch_output,
  output OverFlow,
  output CarryOut
);

  wire alu_1_bit_1_carryout, alu_1_bit_2_carryout, alu_1_bit_3_carryout, alu_1_bit_4_carryout,
       alu_1_bit_5_carryout, alu_1_bit_6_carryout, alu_1_bit_7_carryout, alu_1_bit_8_carryout,
       alu_1_bit_9_carryout, alu_1_bit_10_carryout, alu_1_bit_11_carryout, alu_1_bit_12_carryout,
       alu_1_bit_13_carryout, alu_1_bit_14_carryout, alu_1_bit_15_carryout, alu_1_bit_16_carryout,
       alu_1_bit_17_carryout, alu_1_bit_18_carryout, alu_1_bit_19_carryout, alu_1_bit_20_carryout,
       alu_1_bit_21_carryout, alu_1_bit_22_carryout, alu_1_bit_23_carryout, alu_1_bit_24_carryout,
       alu_1_bit_25_carryout, alu_1_bit_26_carryout, alu_1_bit_27_carryout, alu_1_bit_28_carryout,
       alu_1_bit_29_carryout, alu_1_bit_30_carryout, alu_1_bit_31_carryout, and_1_out, B6, comparator_1_eq,
       comparator_1_gt, comparator_1_lt, comparator_2_eq, comparator_2_gt, comparator_2_lt, comparator_3_eq,
       comparator_3_gt, comparator_3_lt, comparator_4_gt, comparator_4_lt, not_2_out, not_3_out, not_4_out,
       not_5_out, not_6_out, slt_out, sltu_out, Zero_Flag;
  wire [31:0] bit_extender_3_out, bit_extender_4_out, bit_extender_5_out, Result, shifter_1_out,
       shifter_2_out, shifter_3_out, shifter_4_out;
  wire [63:0] bit_extender_1_out, bit_extender_2_out, multiplier_1_out;

  // Probe on {in_4[15:7], in_2[6], in_4[5:0]}
  // Probe on in_2
  and and_1 (and_1_out, Result[1], Result[2], Result[3], Result[4], Result[5], Result[6], Result[7], Result[8], Result[9], Result[10], Result[11], Result[12], Result[13], Result[14], Result[14], Result[15], Result[16], Result[17], Result[18], Result[19], Result[20], Result[21], Result[22], Result[23], Result[24], Result[25], Result[26], Result[27], Result[28], Result[29], Result[30], Result[31]);
  not not_1 (Zero_Flag, and_1_out);
  // Probe on in_4[4:0]
  // Probe on Zero_Flag
  Alu_1_bit alu_1_bit_1 (
    .BInvert(AInvert), .AInvert(BInvert), .CarryIn(CarryIn), .Operation(Operation), .A(in_2[0]), .B(in_4[0]),
    .CarryOut(alu_1_bit_1_carryout), .Result(Result[0]));
  Alu_1_bit alu_1_bit_2 (
    .BInvert(AInvert), .AInvert(BInvert), .CarryIn(alu_1_bit_1_carryout), .Operation(Operation), .A(in_2[1]),
    .B(in_4[1]), .CarryOut(alu_1_bit_2_carryout), .Result(Result[1]));
  Alu_1_bit alu_1_bit_3 (
    .BInvert(AInvert), .AInvert(BInvert), .CarryIn(alu_1_bit_2_carryout), .Operation(Operation), .A(in_2[2]),
    .B(in_4[2]), .CarryOut(alu_1_bit_3_carryout), .Result(Result[2]));
  Alu_1_bit alu_1_bit_4 (
    .BInvert(AInvert), .AInvert(BInvert), .CarryIn(alu_1_bit_3_carryout), .Operation(Operation), .A(in_2[3]),
    .B(in_4[3]), .CarryOut(alu_1_bit_4_carryout), .Result(Result[3]));
  Alu_1_bit alu_1_bit_5 (
    .BInvert(AInvert), .AInvert(BInvert), .CarryIn(alu_1_bit_4_carryout), .Operation(Operation), .A(in_2[4]),
    .B(in_4[4]), .CarryOut(alu_1_bit_5_carryout), .Result(Result[4]));
  Alu_1_bit alu_1_bit_6 (
    .BInvert(AInvert), .AInvert(BInvert), .CarryIn(alu_1_bit_5_carryout), .Operation(Operation), .A(in_2[5]),
    .B(in_4[5]), .CarryOut(alu_1_bit_6_carryout), .Result(Result[5]));
  Alu_1_bit alu_1_bit_7 (
    .BInvert(AInvert), .AInvert(BInvert), .CarryIn(alu_1_bit_6_carryout), .Operation(Operation), .A(in_2[6]),
    .B(B6), .CarryOut(alu_1_bit_7_carryout), .Result(Result[6]));
  Alu_1_bit alu_1_bit_8 (
    .BInvert(AInvert), .AInvert(BInvert), .CarryIn(alu_1_bit_7_carryout), .Operation(Operation), .A(in_2[7]),
    .B(in_4[7]), .CarryOut(alu_1_bit_8_carryout), .Result(Result[7]));
  Alu_1_bit alu_1_bit_9 (
    .BInvert(AInvert), .AInvert(BInvert), .CarryIn(alu_1_bit_8_carryout), .Operation(Operation), .A(in_2[8]),
    .B(in_4[8]), .CarryOut(alu_1_bit_9_carryout), .Result(Result[8]));
  Alu_1_bit alu_1_bit_10 (
    .BInvert(AInvert), .AInvert(BInvert), .CarryIn(alu_1_bit_9_carryout), .Operation(Operation), .A(in_2[9]),
    .B(in_4[9]), .CarryOut(alu_1_bit_10_carryout), .Result(Result[9]));
  Alu_1_bit alu_1_bit_11 (
    .BInvert(AInvert), .AInvert(BInvert), .CarryIn(alu_1_bit_10_carryout), .Operation(Operation),
    .A(in_2[10]), .B(in_4[10]), .CarryOut(alu_1_bit_11_carryout), .Result(Result[10]));
  Alu_1_bit alu_1_bit_12 (
    .BInvert(AInvert), .AInvert(BInvert), .CarryIn(alu_1_bit_11_carryout), .Operation(Operation),
    .A(in_2[11]), .B(in_4[11]), .CarryOut(alu_1_bit_12_carryout), .Result(Result[11]));
  Alu_1_bit alu_1_bit_13 (
    .BInvert(AInvert), .AInvert(BInvert), .CarryIn(alu_1_bit_12_carryout), .Operation(Operation),
    .A(in_2[12]), .B(in_4[12]), .CarryOut(alu_1_bit_13_carryout), .Result(Result[12]));
  Alu_1_bit alu_1_bit_14 (
    .BInvert(AInvert), .AInvert(BInvert), .CarryIn(alu_1_bit_13_carryout), .Operation(Operation),
    .A(in_2[13]), .B(in_4[13]), .CarryOut(alu_1_bit_14_carryout), .Result(Result[13]));
  Alu_1_bit alu_1_bit_15 (
    .BInvert(AInvert), .AInvert(BInvert), .CarryIn(alu_1_bit_14_carryout), .Operation(Operation),
    .A(in_2[14]), .B(in_4[14]), .CarryOut(alu_1_bit_15_carryout), .Result(Result[14]));
  Alu_1_bit alu_1_bit_16 (
    .BInvert(AInvert), .AInvert(BInvert), .CarryIn(alu_1_bit_15_carryout), .Operation(Operation),
    .A(in_2[15]), .B(in_4[15]), .CarryOut(alu_1_bit_16_carryout), .Result(Result[15]));
  Alu_1_bit alu_1_bit_17 (
    .BInvert(AInvert), .AInvert(BInvert), .CarryIn(alu_1_bit_16_carryout), .Operation(Operation),
    .A(in_2[16]), .B(in_4[16]), .CarryOut(alu_1_bit_17_carryout), .Result(Result[16]));
  Alu_1_bit alu_1_bit_18 (
    .BInvert(AInvert), .AInvert(BInvert), .CarryIn(alu_1_bit_17_carryout), .Operation(Operation),
    .A(in_2[17]), .B(in_4[17]), .CarryOut(alu_1_bit_18_carryout), .Result(Result[17]));
  Alu_1_bit alu_1_bit_19 (
    .BInvert(AInvert), .AInvert(BInvert), .CarryIn(alu_1_bit_18_carryout), .Operation(Operation),
    .A(in_2[18]), .B(in_4[18]), .CarryOut(alu_1_bit_19_carryout), .Result(Result[18]));
  Alu_1_bit alu_1_bit_20 (
    .BInvert(AInvert), .AInvert(BInvert), .CarryIn(alu_1_bit_19_carryout), .Operation(Operation),
    .A(in_2[19]), .B(in_4[19]), .CarryOut(alu_1_bit_20_carryout), .Result(Result[19]));
  Alu_1_bit alu_1_bit_21 (
    .BInvert(AInvert), .AInvert(BInvert), .CarryIn(alu_1_bit_20_carryout), .Operation(Operation),
    .A(in_2[20]), .B(in_4[20]), .CarryOut(alu_1_bit_21_carryout), .Result(Result[20]));
  Alu_1_bit alu_1_bit_22 (
    .BInvert(AInvert), .AInvert(BInvert), .CarryIn(alu_1_bit_21_carryout), .Operation(Operation),
    .A(in_2[21]), .B(in_4[21]), .CarryOut(alu_1_bit_22_carryout), .Result(Result[21]));
  Alu_1_bit alu_1_bit_23 (
    .BInvert(AInvert), .AInvert(BInvert), .CarryIn(alu_1_bit_22_carryout), .Operation(Operation),
    .A(in_2[22]), .B(in_4[22]), .CarryOut(alu_1_bit_23_carryout), .Result(Result[22]));
  Alu_1_bit alu_1_bit_24 (
    .BInvert(AInvert), .AInvert(BInvert), .CarryIn(alu_1_bit_23_carryout), .Operation(Operation),
    .A(in_2[23]), .B(in_4[23]), .CarryOut(alu_1_bit_24_carryout), .Result(Result[23]));
  Alu_1_bit alu_1_bit_25 (
    .BInvert(AInvert), .AInvert(BInvert), .CarryIn(alu_1_bit_24_carryout), .Operation(Operation),
    .A(in_2[24]), .B(in_4[24]), .CarryOut(alu_1_bit_25_carryout), .Result(Result[24]));
  Alu_1_bit alu_1_bit_26 (
    .BInvert(AInvert), .AInvert(BInvert), .CarryIn(alu_1_bit_25_carryout), .Operation(Operation),
    .A(in_2[25]), .B(in_4[25]), .CarryOut(alu_1_bit_26_carryout), .Result(Result[25]));
  Alu_1_bit alu_1_bit_27 (
    .BInvert(AInvert), .AInvert(BInvert), .CarryIn(alu_1_bit_26_carryout), .Operation(Operation),
    .A(in_2[26]), .B(in_4[26]), .CarryOut(alu_1_bit_27_carryout), .Result(Result[26]));
  Alu_1_bit alu_1_bit_28 (
    .BInvert(AInvert), .AInvert(BInvert), .CarryIn(alu_1_bit_27_carryout), .Operation(Operation),
    .A(in_2[27]), .B(in_4[27]), .CarryOut(alu_1_bit_28_carryout), .Result(Result[27]));
  Alu_1_bit alu_1_bit_29 (
    .BInvert(AInvert), .AInvert(BInvert), .CarryIn(alu_1_bit_28_carryout), .Operation(Operation),
    .A(in_2[28]), .B(in_4[28]), .CarryOut(alu_1_bit_29_carryout), .Result(Result[28]));
  Alu_1_bit alu_1_bit_30 (
    .BInvert(AInvert), .AInvert(BInvert), .CarryIn(alu_1_bit_29_carryout), .Operation(Operation),
    .A(in_2[29]), .B(in_4[29]), .CarryOut(alu_1_bit_30_carryout), .Result(Result[29]));
  Alu_1_bit alu_1_bit_31 (
    .BInvert(AInvert), .AInvert(BInvert), .CarryIn(alu_1_bit_30_carryout), .Operation(Operation),
    .A(in_2[30]), .B(in_4[30]), .CarryOut(alu_1_bit_31_carryout), .Result(Result[30]));
  Alu_1_bit alu_1_bit_32 (
    .BInvert(AInvert), .AInvert(BInvert), .CarryIn(alu_1_bit_31_carryout), .Operation(Operation),
    .A(in_2[31]), .B(in_4[31]), .CarryOut(CarryOut), .Result(Result[31]));
  xor xor_1 (OverFlow, alu_1_bit_31_carryout, CarryOut);
  Shifter #(.width(32)) shifter_1 (.in(in_2), .\dist (in_4[4:0]), .out(shifter_1_out));
  Shifter #(.shift("lr"), .width(32)) shifter_2 (.in(in_2), .\dist (in_4[4:0]), .out(shifter_2_out));
  Shifter #(.shift("ar"), .width(32)) shifter_3 (.in(in_2), .\dist (in_4[4:0]), .out(shifter_3_out));
  Shifter #(.shift("ar"), .width(32)) shifter_4 (.in(in_2), .\dist (in_4[4:0]), .out(shifter_4_out));
  Comparator #(.mode("unsigned"), .width(32)) comparator_1 (
    .a(in_2), .b({in_4[31:7], in_2[6], in_4[5:0]}), .gt(comparator_1_gt), .eq(comparator_1_eq),
    .lt(comparator_1_lt));
  Comparator #(.width(32)) comparator_2 (
    .a(in_2), .b({in_4[31:7], in_2[6], in_4[5:0]}), .gt(comparator_2_gt), .eq(comparator_2_eq),
    .lt(comparator_2_lt));
  assign bit_extender_1_out = {{32{in_2[31]}}, in_2};  // Bit_Extender bit_extender_1
  assign bit_extender_2_out = {{32{in_4[31]}}, {in_4[31:7], in_2[6], in_4[5:0]}};  // Bit_Extender bit_extender_2
  Comparator #(.width(32)) comparator_3 (
    .a(in_2), .b({in_4[31:7], in_2[6], in_4[5:0]}), .gt(comparator_3_gt), .eq(comparator_3_eq),
    .lt(comparator_3_lt));
  Comparator #(.mode("unsigned"), .width(32)) comparator_4 (
    .a(in_2), .b({in_4[31:7], in_2[6], in_4[5:0]}), .gt(comparator_4_gt), .lt(comparator_4_lt));  // open: eq
  assign bit_extender_3_out = {{31{1'b0}}, comparator_2_eq};  // Bit_Extender bit_extender_3
  not not_2 (not_2_out, comparator_1_gt);
  not not_3 (not_3_out, comparator_1_eq);
  not not_4 (not_4_out, comparator_2_gt);
  not not_5 (not_5_out, comparator_2_eq);
  Multiplier #(.width(64)) multiplier_1 (
    .a(bit_extender_1_out), .b(bit_extender_2_out), .out(multiplier_1_out));  // open: cin, cout
  and sltu (sltu_out, not_2_out, not_3_out, comparator_1_lt);
  and slt (slt_out, not_4_out, not_5_out, comparator_2_lt);
  assign bit_extender_4_out = {{31{1'b0}}, sltu_out};  // Bit_Extender bit_extender_4
  assign bit_extender_5_out = {{31{1'b0}}, slt_out};  // Bit_Extender bit_extender_5
  Multiplexer #(.select(4), .width(32)) multiplexer_1 (
    .in4(Result), .in5(shifter_1_out), .in6(shifter_2_out), .in7(shifter_3_out), .in8(shifter_4_out),
    .in9(bit_extender_4_out), .in10(bit_extender_5_out), .in11(bit_extender_3_out),
    .in12({in_4[31:7], in_2[6], in_4[5:0]}), .in13({Alu_Result[15:0], in_4[15:7], in_2[6], in_4[5:0]}),
    .in14(multiplier_1_out[31:0]), .out(Alu_Result), .sel(select_Alu));  // open: in0, in1, in2, in3, in15
  not not_6 (not_6_out, comparator_3_eq);
  Multiplexer #(.enable("true"), .select(3)) multiplexer_2 (
    .in0(comparator_3_eq), .in3(not_6_out), .in4(comparator_3_gt), .in5(comparator_3_lt),
    .in6(comparator_4_gt), .in7(comparator_4_lt), .out(branch_output), .sel(Branching));  // open: in1, in2, en

  assign in_4[6] = in_2[6];

  // Other names for the same wires on the sheet: B[31:0] = {in_4[31:7], in_2[6], in_4[5:0]}; B0 = in_4[0];
  //   least_significant_5_bits_of_B[4:0] = in_4[4:0];
  //   least_significant_16_bits_of_B[15:0] = {in_4[15:7], in_2[6], in_4[5:0]}; B1 = in_4[1]; B2 = in_4[2];
  //   B3 = in_4[3]; B4 = in_4[4]; B5 = in_4[5]; A[31:0] = in_2; A6 = in_2[6]; B7 = in_4[7]; B8 = in_4[8];
  //   B9 = in_4[9]; B10 = in_4[10]; B11 = in_4[11]; B12 = in_4[12]; B13 = in_4[13]; B14 = in_4[14]; B15 = in_4[15];
  //   A0 = in_2[0]; A1 = in_2[1]; A2 = in_2[2]; A3 = in_2[3]; A4 = in_2[4]; A5 = in_2[5]; A7 = in_2[7]; A8 = in_2[8];
  //   A9 = in_2[9]; A10 = in_2[10]; A11 = in_2[11]; A12 = in_2[12]; A13 = in_2[13]; A14 = in_2[14]; A15 = in_2[15];
  //   A16 = in_2[16]; A17 = in_2[17]; A18 = in_2[18]; A19 = in_2[19]; A20 = in_2[20]; A21 = in_2[21]; A22 = in_2[22];
  //   A23 = in_2[23]; A24 = in_2[24]; A25 = in_2[25]; A26 = in_2[26]; A27 = in_2[27]; A28 = in_2[28]; A29 = in_2[29];
  //   A30 = in_2[30]; A31 = in_2[31]; B16 = in_4[16]; B17 = in_4[17]; B18 = in_4[18]; B19 = in_4[19]; B20 = in_4[20];
  //   B21 = in_4[21]; B22 = in_4[22]; B23 = in_4[23]; B24 = in_4[24]; B25 = in_4[25]; B26 = in_4[26]; B27 = in_4[27];
  //   B28 = in_4[28]; B29 = in_4[29]; B30 = in_4[30]; B31 = in_4[31]; Rs0 = Result[0]; Rs1 = Result[1];
  //   Rs2 = Result[2]; Rs3 = Result[3]; Rs4 = Result[4]; Rs5 = Result[5]; Rs6 = Result[6]; Rs7 = Result[7];
  //   Rs8 = Result[8]; Rs9 = Result[9]; Rs10 = Result[10]; Rs11 = Result[11]; Rs12 = Result[12]; Rs13 = Result[13];
  //   Rs14 = Result[14]; Rs15 = Result[15]; Rs16 = Result[16]; Rs17 = Result[17]; Rs18 = Result[18];
  //   Rs19 = Result[19]; Rs20 = Result[20]; Rs21 = Result[21]; Rs22 = Result[22]; Rs23 = Result[23];
  //   Rs24 = Result[24]; Rs25 = Result[25]; Rs26 = Result[26]; Rs27 = Result[27]; Rs28 = Result[28];
  //   Rs29 = Result[29]; Rs30 = Result[30]; Rs31 = Result[31]

  // Notes on the sheet:
  //   unsigned
  //   signed
  //   set
  //   signed
  //   unsigned
  //   seteq
  //   old_rd
  //   sset
endmodule

module Alu_1_bit (
  input  A,
  input  B,
  input  CarryIn,
  input  BInvert,
  input  AInvert,
  input  [1:0] Operation,
  output Result,
  output CarryOut
);

  wire adder_1_out, and_1_out, multiplexer_1_out, multiplexer_2_out, not_1_out, not_2_out, or_1_out,
       xor_1_out;

  not not_1 (not_1_out, A);
  not not_2 (not_2_out, B);
  Multiplexer #(.enable("true")) multiplexer_1 (
    .in0(A), .in1(not_1_out), .out(multiplexer_1_out), .sel(AInvert));  // open: en
  Multiplexer #(.enable("true")) multiplexer_2 (
    .in0(B), .in1(not_2_out), .out(multiplexer_2_out), .sel(BInvert));  // open: en
  and and_1 (and_1_out, multiplexer_1_out, multiplexer_2_out);
  or or_1 (or_1_out, multiplexer_1_out, multiplexer_2_out);
  xor xor_1 (xor_1_out, multiplexer_1_out, multiplexer_2_out);
  Adder #(.width(1)) adder_1 (
    .a(multiplexer_1_out), .b(multiplexer_2_out), .out(adder_1_out), .cin(CarryIn), .cout(CarryOut));
  Multiplexer #(.enable("true"), .select(2)) multiplexer_3 (
    .in0(and_1_out), .in1(or_1_out), .in2(xor_1_out), .in3(adder_1_out), .out(Result), .sel(Operation));  // open: en
endmodule
