// Logisim project ALU1Bit.circ as structural Verilog
module ALU (
  input  [31:0] in_1,
  input  [31:0] in_2,
  input  A,
  input  B,
  input  [2:0] select_Alu,
  input  CarryIn,
  input  [31:0] in_7,
  input  BInvert,
  input  AInvert,
  input  [1:0] Operation,
  output [31:0] Alu_Result,
  output Result,
  output out_13
);

  wire adder_1_cout, adder_1_out, and_1_out, and_2_out, and_3_out, and_4_out, comparator_1_eq,
       comparator_1_gt, comparator_1_lt, comparator_2_eq, comparator_2_gt, comparator_2_lt,
       multiplexer_1_out, multiplexer_2_out, not_1_out, not_2_out, not_3_out, not_4_out, not_5_out,
       not_6_out, or_1_out, xor_1_out;
  wire [31:0] bit_extender_1_out, bit_extender_2_out, shifter_1_out, shifter_2_out, shifter_3_out,
       shifter_4_out;

  not not_1 (not_1_out, A);
  not not_2 (not_2_out, B);
  Multiplexer multiplexer_1 (.in0(A), .in1(not_1_out), .out(multiplexer_1_out), .sel(AInvert));
  Multiplexer multiplexer_2 (.in0(B), .in1(not_2_out), .out(multiplexer_2_out), .sel(BInvert));
  and and_1 (and_1_out, multiplexer_1_out, multiplexer_2_out);
  or or_1 (or_1_out, multiplexer_1_out, multiplexer_2_out);
  xor xor_1 (xor_1_out, multiplexer_1_out, multiplexer_2_out);
  Adder #(.width(1)) adder_1 (
    .a(multiplexer_1_out), .b(multiplexer_2_out), .out(adder_1_out), .cin(CarryIn), .cout(adder_1_cout));
  // Probe on adder_1_cout
  Multiplexer #(.select(2)) multiplexer_3 (
    .in0(and_1_out), .in1(or_1_out), .in2(xor_1_out), .in3(adder_1_out), .out(Result), .sel(Operation));
  Shifter #(.width(32)) shifter_1 (.in(in_1), .\dist (in_7[4:0]), .out(shifter_1_out));
  Shifter #(.shift("lr"), .width(32)) shifter_2 (.in(in_1), .\dist (in_7[4:0]), .out(shifter_2_out));
  Shifter #(.shift("ar"), .width(32)) shifter_3 (.in(in_1), .\dist (in_7[4:0]), .out(shifter_3_out));
  Shifter #(.shift("ar"), .width(32)) shifter_4 (.in(in_1), .\dist (in_7[4:0]), .out(shifter_4_out));
  Comparator #(.mode("unsigned"), .width(32)) comparator_1 (
    .a(in_1), .b({in_7[31:7], in_1[6], in_7[5:0]}), .gt(comparator_1_gt), .eq(comparator_1_eq),
    .lt(comparator_1_lt));
  Comparator #(.width(32)) comparator_2 (
    .a(in_1), .b({in_7[31:7], in_1[6], in_7[5:0]}), .gt(comparator_2_gt), .eq(comparator_2_eq),
    .lt(comparator_2_lt));
  not not_3 (not_3_out, comparator_1_gt);
  not not_4 (not_4_out, comparator_1_eq);
  not not_5 (not_5_out, comparator_2_gt);
  not not_6 (not_6_out, comparator_2_eq);
  and and_2 (and_2_out, in_2[0], in_2[1], in_2[2], in_2[3], in_2[4], in_2[5], in_2[6], in_2[7], in_2[8], in_2[9], in_2[10], in_2[11], in_2[12], in_2[14], in_2[14], in_2[15], in_2[16], in_2[17], in_2[18], in_2[19], in_2[20], in_2[21], in_2[22], in_2[23], in_2[24], in_2[25], in_2[26], in_2[27], in_2[28], in_2[29], in_2[30], in_2[31]);
  assign bit_extender_1_out = {{31{and_3_out}}, and_3_out};  // Bit_Extender bit_extender_1
  and and_3 (and_3_out, not_3_out, not_4_out, comparator_1_lt);
  assign bit_extender_2_out = {{31{and_4_out}}, and_4_out};  // Bit_Extender bit_extender_2
  and and_4 (and_4_out, not_5_out, not_6_out, comparator_2_lt);
  not not_7 (out_13, and_2_out);
  Multiplexer #(.select(3), .width(32)) multiplexer_4 (
    .in0({in_2[31:14], in_2[14], in_2[12:0]}), .in1(shifter_1_out), .in2(shifter_2_out), .in3(shifter_3_out),
    .in4(shifter_4_out), .in5(bit_extender_1_out), .in6(bit_extender_2_out), .out(Alu_Result),
    .sel(select_Alu));  // open: in7

  assign in_2[13] = in_2[14];
  assign in_7[6] = in_1[6];

  // Other names for the same wires on the sheet: A0 = in_1[0]; A_t[31:0] = in_1; A1 = in_1[1]; A2 = in_1[2];
  //   A3 = in_1[3]; A4 = in_1[4]; A5 = in_1[5]; A7 = in_1[7]; A8 = in_1[8]; A9 = in_1[9]; A10 = in_1[10];
  //   A11 = in_1[11]; A12 = in_1[12]; A13 = in_1[13]; A14 = in_1[14]; A15 = in_1[15]; A16 = in_1[16]; A17 = in_1[17];
  //   A18 = in_1[18]; A19 = in_1[19]; A20 = in_1[20]; A21 = in_1[21]; A22 = in_1[22]; A23 = in_1[23]; A24 = in_1[24];
  //   A25 = in_1[25]; A26 = in_1[26]; A27 = in_1[27]; A28 = in_1[28]; A29 = in_1[29]; A30 = in_1[30]; A31 = in_1[31];
  //   B0 = in_7[0]; B_t[31:0] = {in_7[31:7], in_1[6], in_7[5:0]}; least_significant_5_bits_of_B[4:0] = in_7[4:0];
  //   B1 = in_7[1]; B2 = in_7[2]; B3 = in_7[3]; B4 = in_7[4]; B5 = in_7[5]; A6 = in_1[6]; B7 = in_7[7]; B8 = in_7[8];
  //   B9 = in_7[9]; B10 = in_7[10]; B11 = in_7[11]; B12 = in_7[12]; B13 = in_7[13]; B14 = in_7[14]; B15 = in_7[15];
  //   B16 = in_7[16]; B17 = in_7[17]; B18 = in_7[18]; B19 = in_7[19]; B20 = in_7[20]; B21 = in_7[21]; B22 = in_7[22];
  //   B23 = in_7[23]; B24 = in_7[24]; B25 = in_7[25]; B26 = in_7[26]; B27 = in_7[27]; B28 = in_7[28]; B29 = in_7[29];
  //   B30 = in_7[30]; B31 = in_7[31]; Result_t[31:0] = {in_2[31:14], in_2[14], in_2[12:0]}; Rs1 = in_2[0];
  //   Rs2 = in_2[1]; Rs3 = in_2[2]; Rs4 = in_2[3]; Rs5 = in_2[4]; Rs6 = in_2[5]; Rs7 = in_2[6]; Rs8 = in_2[7];
  //   Rs9 = in_2[8]; Rs10 = in_2[9]; Rs11 = in_2[10]; Rs12 = in_2[11]; Rs13 = in_2[12]; Rs14 = in_2[14];
  //   Rs15 = in_2[15]; Rs16 = in_2[16]; Rs17 = in_2[17]; Rs18 = in_2[18]; Rs19 = in_2[19]; Rs20 = in_2[20];
  //   Rs21 = in_2[21]; Rs22 = in_2[22]; Rs23 = in_2[23]; Rs24 = in_2[24]; Rs25 = in_2[25]; Rs26 = in_2[26];
  //   Rs27 = in_2[27]; Rs28 = in_2[28]; Rs29 = in_2[29]; Rs30 = in_2[30]; Rs31 = in_2[31]
endmodule
