// Logisim project ALUcontrol.circ as structural Verilog: 1 circuit, main circuit main
module main (
  output [7:0] ALU_Op
);

  wire ADD, ADDI, BEQ, BGE, BGEU, BLT, BLTU, BNE, LW, MUL, NOR, NORI, OR, ORI, ROR, RORI, SEQ, SEQI, SET,
       SLL, SLLI, SLT, SLTI, SLTIU, SLTU, SRA, SRAI, SRL, SRLI, SSET, SUB, SW, XOR, XORI;

  or Bit_3 (ALU_Op[3], SET, SSET);
  or Bit_6 (ALU_Op[6], SUB, NOR, NORI, BEQ, BNE);
  or Bit_7 (ALU_Op[7], NOR, NORI);
  or Bit_0 (ALU_Op[0], SLL, SRA, SLTU, SEQ, SLLI, SRAI, SLTIU, SEQI, SSET, BLTU, BGEU);
  or bit_1 (ALU_Op[1], SRL, SRA, SEQ, SRLI, SLTI, SRAI, MUL, SEQI, BLT, BGE, SLT);
  or Bit2 (ALU_Op[2], ROR, SLT, SLTU, SEQ, RORI, SLTI, SLTIU, SEQI, BLT, BGE, BLTU, BGEU);
  or Bit_4 (ALU_Op[4], ADD, SUB, OR, ADDI, ORI, LW, SW, BEQ, BNE);
  or Bit_5 (ALU_Op[5], ADD, SUB, XOR, ADDI, XORI, LW, SW, BEQ, BNE);

  // Notes on the sheet:
  //   ALU_Op
endmodule
