// Logisim project EX_MEM_Register.circ as structural Verilog: 1 circuit, main circuit main
module main (
  input  in_1,
  input  [31:0] ALU_result_EX,
  input  [31:0] BusB_EX,
  input  MemRead_EX,
  input  MemWrite_EX,
  input  MemtoReg_EX,
  input  RegWrite_EX,
  input  [4:0] Reg_Des_EX,
  input  [19:0] pc_inc_EX,
  input  jalr_EX,
  input  [15:0] Imm16_EX,
  input  Sset_EX,
  output [31:0] ALU_result_MEM,
  output [31:0] BusB_MEM,
  output MemRead_MEM,
  output MemWrite_MEM,
  output MemtoReg_MEM,
  output RegWrite_MEM,
  output [4:0] Reg_Des_MEM,
  output [19:0] pc_inc_MEM,
  output jalr_MEM,
  output Sset_MEM,
  output [15:0] Imm16_MEM
);

  wire undriven, undriven_2;

  Register #(.width(16)) register_1 (.D(Imm16_EX), .en(1'b1), .clk(in_1), .Q(Imm16_MEM));  // open: clr
  Register #(.width(32)) register_2 (.D(ALU_result_EX), .en(1'b1), .clk(in_1), .Q(ALU_result_MEM));  // open: clr
  Register #(.width(1)) register_3 (.D(MemRead_EX), .en(1'b1), .clk(in_1), .Q(MemRead_MEM));  // open: clr
  Register #(.width(1)) register_4 (.D(MemtoReg_EX), .en(1'b1), .clk(in_1), .Q(MemtoReg_MEM));  // open: clr
  Register #(.width(5)) register_5 (.D(Reg_Des_EX), .en(1'b1), .clk(in_1), .Q(Reg_Des_MEM));  // open: clr
  Register #(.width(20)) register_6 (.D(pc_inc_EX), .en(1'b1), .clk(in_1), .Q(pc_inc_MEM));  // open: clr
  Register #(.width(1)) register_7 (.D(Sset_EX), .en(1'b1), .clk(in_1), .Q(Sset_MEM));  // open: clr
  Register #(.width(32)) register_8 (.D(BusB_EX), .en(1'b1), .clk(in_1), .Q(BusB_MEM), .clr(undriven));
  Register #(.width(1)) register_9 (.D(MemWrite_EX), .en(1'b1), .clk(in_1), .Q(MemWrite_MEM), .clr(undriven_2));
  Register #(.width(1)) register_10 (.D(RegWrite_EX), .en(1'b1), .clk(in_1), .Q(RegWrite_MEM));  // open: clr
  Register #(.width(1)) register_11 (.D(jalr_EX), .en(1'b1), .clk(in_1), .Q(jalr_MEM));  // open: clr

  // Other names for the same wires on the sheet: CLK = in_1
endmodule
