// Logisim project FINALFINAL__ALU.circ as structural Verilog
module ALU1Bit (
  input  A,
  input  B,
  input  CarryIn,
  input  BInvert,
  input  AInvert,
  input  [1:0] Operation,
  output Result,
  output CarryOut
);

  wire adder_1_out, and_1_out, multiplexer_1_out, multiplexer_2_out, not_1_out, not_2_out, or_1_out,
       xor_1_out;

  not not_1 (not_1_out, A);
  not not_2 (not_2_out, B);
  Multiplexer #(.enable("false")) multiplexer_1 (.in0(A), .in1(not_1_out), .out(multiplexer_1_out), .sel(AInvert));
  Multiplexer #(.enable("false")) multiplexer_2 (.in0(B), .in1(not_2_out), .out(multiplexer_2_out), .sel(BInvert));
  and and_1 (and_1_out, multiplexer_1_out, multiplexer_2_out);
  or or_1 (or_1_out, multiplexer_1_out, multiplexer_2_out);
  xor xor_1 (xor_1_out, multiplexer_1_out, multiplexer_2_out);
  Adder #(.width(1)) adder_1 (
    .a(multiplexer_1_out), .b(multiplexer_2_out), .out(adder_1_out), .cin(CarryIn), .cout(CarryOut));
  Multiplexer #(.select(2), .enable("false")) multiplexer_3 (
    .in0(and_1_out), .in1(or_1_out), .in2(xor_1_out), .in3(adder_1_out), .out(Result), .sel(Operation));
endmodule

module ALU_Full (
  input  CarryIn,
  input  [31:0] in_2,
  input  [3:0] select_Alu,
  input  [31:0] in_4,
  input  [31:0] in_5,
  input  [2:0] Branching,
  input  [1:0] Operation,
  input  BInvert,
  input  AInvert,
  output [31:0] Alu_Result,
  output branch_output,
  output OverFlow,
  output CarryOut
);

  wire alu1bit_1_carryout, alu1bit_2_carryout, alu1bit_3_carryout, alu1bit_4_carryout, alu1bit_5_carryout,
       alu1bit_6_carryout, alu1bit_7_carryout, alu1bit_8_carryout, alu1bit_9_carryout, alu1bit_10_carryout,
       alu1bit_11_carryout, alu1bit_12_carryout, alu1bit_13_carryout, alu1bit_14_carryout,
       alu1bit_15_carryout, alu1bit_16_carryout, alu1bit_17_carryout, alu1bit_18_carryout,
       alu1bit_19_carryout, alu1bit_20_carryout, alu1bit_21_carryout, alu1bit_22_carryout,
       alu1bit_23_carryout, alu1bit_24_carryout, alu1bit_25_carryout, alu1bit_26_carryout,
       alu1bit_27_carryout, alu1bit_28_carryout, alu1bit_29_carryout, alu1bit_30_carryout,
       alu1bit_31_carryout, and_1_out, comparator_1_eq, comparator_1_gt, comparator_1_lt, comparator_2_eq,
       comparator_2_gt, comparator_2_lt, comparator_3_gt, comparator_4_gt, less_sign_flag, less_unsign_flag,
       not_2_out, not_3_out, not_4_out, not_5_out, not_6_out, slt_out, sltu_out, Zero_Flag;
  wire [30:0] multiplier_1_out;
  wire [31:0] bit_extender_1_out, bit_extender_2_out, bit_extender_3_out, bit_extender_4_out, Result,
       shifter_1_out, shifter_2_out, shifter_3_out, shifter_4_out;

  // Probe on in_4
  // Probe on in_2
  // Probe on in_4[4:0]
  and and_1 (and_1_out, Result[1], Result[2], Result[3], Result[4], Result[5], Result[6], Result[7], Result[8], Result[9], Result[10], Result[11], Result[12], Result[13], Result[14], Result[14], Result[15], Result[16], Result[17], Result[18], Result[19], Result[20], Result[21], Result[22], Result[23], Result[24], Result[25], Result[26], Result[27], Result[28], Result[29], Result[30], Result[31]);
  not not_1 (Zero_Flag, and_1_out);
  // Probe on Zero_Flag
  ALU1Bit alu1bit_1 (
    .A(in_2[0]), .B(in_4[0]), .Result(Result[0]), .CarryIn(CarryIn), .BInvert(BInvert), .AInvert(AInvert),
    .CarryOut(alu1bit_1_carryout), .Operation(Operation));
  ALU1Bit alu1bit_2 (
    .A(in_2[1]), .B(in_4[1]), .Result(Result[1]), .CarryIn(alu1bit_1_carryout), .BInvert(BInvert),
    .AInvert(AInvert), .CarryOut(alu1bit_2_carryout), .Operation(Operation));
  ALU1Bit alu1bit_3 (
    .A(in_2[2]), .B(in_4[2]), .Result(Result[2]), .CarryIn(alu1bit_2_carryout), .BInvert(BInvert),
    .AInvert(AInvert), .CarryOut(alu1bit_3_carryout), .Operation(Operation));
  ALU1Bit alu1bit_4 (
    .A(in_2[3]), .B(in_4[3]), .Result(Result[3]), .CarryIn(alu1bit_3_carryout), .BInvert(BInvert),
    .AInvert(AInvert), .CarryOut(alu1bit_4_carryout), .Operation(Operation));
  ALU1Bit alu1bit_5 (
    .A(in_2[4]), .B(in_4[4]), .Result(Result[4]), .CarryIn(alu1bit_4_carryout), .BInvert(BInvert),
    .AInvert(AInvert), .CarryOut(alu1bit_5_carryout), .Operation(Operation));
  ALU1Bit alu1bit_6 (
    .A(in_2[5]), .B(in_4[5]), .Result(Result[5]), .CarryIn(alu1bit_5_carryout), .BInvert(BInvert),
    .AInvert(AInvert), .CarryOut(alu1bit_6_carryout), .Operation(Operation));
  ALU1Bit alu1bit_7 (
    .A(in_2[6]), .B(in_4[6]), .Result(Result[6]), .CarryIn(alu1bit_6_carryout), .BInvert(BInvert),
    .AInvert(AInvert), .CarryOut(alu1bit_7_carryout), .Operation(Operation));
  ALU1Bit alu1bit_8 (
    .A(in_2[7]), .B(in_4[7]), .Result(Result[7]), .CarryIn(alu1bit_7_carryout), .BInvert(BInvert),
    .AInvert(AInvert), .CarryOut(alu1bit_8_carryout), .Operation(Operation));
  ALU1Bit alu1bit_9 (
    .A(in_2[8]), .B(in_4[8]), .Result(Result[8]), .CarryIn(alu1bit_8_carryout), .BInvert(BInvert),
    .AInvert(AInvert), .CarryOut(alu1bit_9_carryout), .Operation(Operation));
  ALU1Bit alu1bit_10 (
    .A(in_2[9]), .B(in_4[9]), .Result(Result[9]), .CarryIn(alu1bit_9_carryout), .BInvert(BInvert),
    .AInvert(AInvert), .CarryOut(alu1bit_10_carryout), .Operation(Operation));
  ALU1Bit alu1bit_11 (
    .A(in_2[10]), .B(in_4[10]), .Result(Result[10]), .CarryIn(alu1bit_10_carryout), .BInvert(BInvert),
    .AInvert(AInvert), .CarryOut(alu1bit_11_carryout), .Operation(Operation));
  ALU1Bit alu1bit_12 (
    .A(in_2[11]), .B(in_4[11]), .Result(Result[11]), .CarryIn(alu1bit_11_carryout), .BInvert(BInvert),
    .AInvert(AInvert), .CarryOut(alu1bit_12_carryout), .Operation(Operation));
  ALU1Bit alu1bit_13 (
    .A(in_2[12]), .B(in_4[12]), .Result(Result[12]), .CarryIn(alu1bit_12_carryout), .BInvert(BInvert),
    .AInvert(AInvert), .CarryOut(alu1bit_13_carryout), .Operation(Operation));
  ALU1Bit alu1bit_14 (
    .A(in_2[13]), .B(in_4[13]), .Result(Result[13]), .CarryIn(alu1bit_13_carryout), .BInvert(BInvert),
    .AInvert(AInvert), .CarryOut(alu1bit_14_carryout), .Operation(Operation));
  ALU1Bit alu1bit_15 (
    .A(in_2[14]), .B(in_4[14]), .Result(Result[14]), .CarryIn(alu1bit_14_carryout), .BInvert(BInvert),
    .AInvert(AInvert), .CarryOut(alu1bit_15_carryout), .Operation(Operation));
  ALU1Bit alu1bit_16 (
    .A(in_2[15]), .B(in_4[15]), .Result(Result[15]), .CarryIn(alu1bit_15_carryout), .BInvert(BInvert),
    .AInvert(AInvert), .CarryOut(alu1bit_16_carryout), .Operation(Operation));
  ALU1Bit alu1bit_17 (
    .A(in_2[16]), .B(in_4[16]), .Result(Result[16]), .CarryIn(alu1bit_16_carryout), .BInvert(BInvert),
    .AInvert(AInvert), .CarryOut(alu1bit_17_carryout), .Operation(Operation));
  ALU1Bit alu1bit_18 (
    .A(in_2[17]), .B(in_4[17]), .Result(Result[17]), .CarryIn(alu1bit_17_carryout), .BInvert(BInvert),
    .AInvert(AInvert), .CarryOut(alu1bit_18_carryout), .Operation(Operation));
  ALU1Bit alu1bit_19 (
    .A(in_2[18]), .B(in_4[18]), .Result(Result[18]), .CarryIn(alu1bit_18_carryout), .BInvert(BInvert),
    .AInvert(AInvert), .CarryOut(alu1bit_19_carryout), .Operation(Operation));
  ALU1Bit alu1bit_20 (
    .A(in_2[19]), .B(in_4[19]), .Result(Result[19]), .CarryIn(alu1bit_19_carryout), .BInvert(BInvert),
    .AInvert(AInvert), .CarryOut(alu1bit_20_carryout), .Operation(Operation));
  ALU1Bit alu1bit_21 (
    .A(in_2[20]), .B(in_4[20]), .Result(Result[20]), .CarryIn(alu1bit_20_carryout), .BInvert(BInvert),
    .AInvert(AInvert), .CarryOut(alu1bit_21_carryout), .Operation(Operation));
  ALU1Bit alu1bit_22 (
    .A(in_2[21]), .B(in_4[21]), .Result(Result[21]), .CarryIn(alu1bit_21_carryout), .BInvert(BInvert),
    .AInvert(AInvert), .CarryOut(alu1bit_22_carryout), .Operation(Operation));
  ALU1Bit alu1bit_23 (
    .A(in_2[22]), .B(in_4[22]), .Result(Result[22]), .CarryIn(alu1bit_22_carryout), .BInvert(BInvert),
    .AInvert(AInvert), .CarryOut(alu1bit_23_carryout), .Operation(Operation));
  ALU1Bit alu1bit_24 (
    .A(in_2[23]), .B(in_4[23]), .Result(Result[23]), .CarryIn(alu1bit_23_carryout), .BInvert(BInvert),
    .AInvert(AInvert), .CarryOut(alu1bit_24_carryout), .Operation(Operation));
  ALU1Bit alu1bit_25 (
    .A(in_2[24]), .B(in_4[24]), .Result(Result[24]), .CarryIn(alu1bit_24_carryout), .BInvert(BInvert),
    .AInvert(AInvert), .CarryOut(alu1bit_25_carryout), .Operation(Operation));
  ALU1Bit alu1bit_26 (
    .A(in_2[25]), .B(in_4[25]), .Result(Result[25]), .CarryIn(alu1bit_25_carryout), .BInvert(BInvert),
    .AInvert(AInvert), .CarryOut(alu1bit_26_carryout), .Operation(Operation));
  ALU1Bit alu1bit_27 (
    .A(in_2[26]), .B(in_4[26]), .Result(Result[26]), .CarryIn(alu1bit_26_carryout), .BInvert(BInvert),
    .AInvert(AInvert), .CarryOut(alu1bit_27_carryout), .Operation(Operation));
  ALU1Bit alu1bit_28 (
    .A(in_2[27]), .B(in_4[27]), .Result(Result[27]), .CarryIn(alu1bit_27_carryout), .BInvert(BInvert),
    .AInvert(AInvert), .CarryOut(alu1bit_28_carryout), .Operation(Operation));
  ALU1Bit alu1bit_29 (
    .A(in_2[28]), .B(in_4[28]), .Result(Result[28]), .CarryIn(alu1bit_28_carryout), .BInvert(BInvert),
    .AInvert(AInvert), .CarryOut(alu1bit_29_carryout), .Operation(Operation));
  ALU1Bit alu1bit_30 (
    .A(in_2[29]), .B(in_4[29]), .Result(Result[29]), .CarryIn(alu1bit_29_carryout), .BInvert(BInvert),
    .AInvert(AInvert), .CarryOut(alu1bit_30_carryout), .Operation(Operation));
  ALU1Bit alu1bit_31 (
    .A(in_2[30]), .B(in_4[30]), .Result(Result[30]), .CarryIn(alu1bit_30_carryout), .BInvert(BInvert),
    .AInvert(AInvert), .CarryOut(alu1bit_31_carryout), .Operation(Operation));
  ALU1Bit alu1bit_32 (
    .A(in_2[31]), .B(in_4[31]), .Result(Result[31]), .CarryIn(alu1bit_31_carryout), .BInvert(BInvert),
    .AInvert(AInvert), .CarryOut(CarryOut), .Operation(Operation));
  xor xor_1 (OverFlow, alu1bit_31_carryout, CarryOut);
  Shifter #(.width(32)) shifter_1 (.in(in_2), .\dist (in_4[4:0]), .out(shifter_1_out));
  Shifter #(.width(32), .shift("lr")) shifter_2 (.in(in_2), .\dist (in_4[4:0]), .out(shifter_2_out));
  Shifter #(.width(32), .shift("ar")) shifter_3 (.in(in_2), .\dist (in_4[4:0]), .out(shifter_3_out));
  Shifter #(.width(32), .shift("rr")) shifter_4 (.in(in_2), .\dist (in_4[4:0]), .out(shifter_4_out));
  Comparator #(.width(32), .mode("unsigned")) comparator_1 (
    .a(in_2), .b(in_4), .gt(comparator_1_gt), .eq(comparator_1_eq), .lt(comparator_1_lt));
  Comparator #(.width(32)) comparator_2 (
    .a(in_2), .b(in_4), .gt(comparator_2_gt), .eq(comparator_2_eq), .lt(comparator_2_lt));
  Comparator #(.width(32)) comparator_3 (.a(in_2), .b(in_4), .gt(comparator_3_gt), .eq(Zero_Flag), .lt(less_sign_flag));
  Comparator #(.width(32), .mode("unsigned")) comparator_4 (
    .a(in_2), .b(in_4), .gt(comparator_4_gt), .lt(less_unsign_flag));  // open: eq
  assign bit_extender_1_out = {{31{1'b0}}, comparator_2_eq};  // Bit_Extender bit_extender_1
  not not_2 (not_2_out, comparator_1_gt);
  not not_3 (not_3_out, comparator_1_eq);
  not not_4 (not_4_out, comparator_2_gt);
  not not_5 (not_5_out, comparator_2_eq);
  Multiplier #(.width(31)) multiplier_1 (.a(in_2[30:0]), .b(in_4[30:0]), .out(multiplier_1_out));  // open: cin, cout
  and sltu (sltu_out, not_2_out, not_3_out, comparator_1_lt);
  and slt (slt_out, not_4_out, not_5_out, comparator_2_lt);
  assign bit_extender_2_out = {{31{1'b0}}, sltu_out};  // Bit_Extender bit_extender_2
  assign bit_extender_3_out = {{31{1'b0}}, slt_out};  // Bit_Extender bit_extender_3
  assign bit_extender_4_out = {{1{multiplier_1_out[30]}}, multiplier_1_out};  // Bit_Extender bit_extender_4
  Multiplexer #(.select(4), .width(32), .enable("false")) multiplexer_1 (
    .in4(Result), .in5(shifter_1_out), .in6(shifter_2_out), .in7(shifter_3_out), .in8(shifter_4_out),
    .in9(bit_extender_2_out), .in10(bit_extender_3_out), .in11(bit_extender_1_out), .in12(in_4),
    .in13({in_5[15:0], in_4[15:0]}), .in14(bit_extender_4_out), .out(Alu_Result), .sel(select_Alu));  // open: in0, in1, in2, in3, in15
  not not_6 (not_6_out, Zero_Flag);
  Multiplexer #(.select(3)) multiplexer_2 (
    .in0(Zero_Flag), .in3(not_6_out), .in4(comparator_3_gt), .in5(less_sign_flag), .in6(comparator_4_gt),
    .in7(less_unsign_flag), .out(branch_output), .sel(Branching));  // open: in1, in2, en

  // Other names for the same wires on the sheet: B[31:0] = in_4; B0 = in_4[0];
  //   least_significant_5_bits_of_B[4:0] = in_4[4:0]; least_significant_16_bits_of_B[15:0] = in_4[15:0]; B1 = in_4[1];
  //   B2 = in_4[2]; B3 = in_4[3]; B4 = in_4[4]; B5 = in_4[5]; B6 = in_4[6]; B7 = in_4[7]; B8 = in_4[8]; B9 = in_4[9];
  //   B10 = in_4[10]; B11 = in_4[11]; B12 = in_4[12]; B13 = in_4[13]; B14 = in_4[14]; B15 = in_4[15]; A[31:0] = in_2;
  //   A0 = in_2[0]; A1 = in_2[1]; A2 = in_2[2]; A3 = in_2[3]; A4 = in_2[4]; A5 = in_2[5]; A6 = in_2[6]; A7 = in_2[7];
  //   A8 = in_2[8]; A9 = in_2[9]; A10 = in_2[10]; A11 = in_2[11]; A12 = in_2[12]; A13 = in_2[13]; A14 = in_2[14];
  //   A15 = in_2[15]; A16 = in_2[16]; A17 = in_2[17]; A18 = in_2[18]; A19 = in_2[19]; A20 = in_2[20]; A21 = in_2[21];
  //   A22 = in_2[22]; A23 = in_2[23]; A24 = in_2[24]; A25 = in_2[25]; A26 = in_2[26]; A27 = in_2[27]; A28 = in_2[28];
  //   A29 = in_2[29]; A30 = in_2[30]; A31 = in_2[31]; B16 = in_4[16]; B17 = in_4[17]; B18 = in_4[18]; B19 = in_4[19];
  //   B20 = in_4[20]; B21 = in_4[21]; B22 = in_4[22]; B23 = in_4[23]; B24 = in_4[24]; B25 = in_4[25]; B26 = in_4[26];
  //   B27 = in_4[27]; B28 = in_4[28]; B29 = in_4[29]; B30 = in_4[30]; B31 = in_4[31]; Rs0 = Result[0];
  //   Rs1 = Result[1]; Rs2 = Result[2]; Rs3 = Result[3]; Rs4 = Result[4]; Rs5 = Result[5]; Rs6 = Result[6];
  //   Rs7 = Result[7]; Rs8 = Result[8]; Rs9 = Result[9]; Rs10 = Result[10]; Rs11 = Result[11]; Rs12 = Result[12];
  //   Rs13 = Result[13]; Rs14 = Result[14]; Rs15 = Result[15]; Rs16 = Result[16]; Rs17 = Result[17];
  //   Rs18 = Result[18]; Rs19 = Result[19]; Rs20 = Result[20]; Rs21 = Result[21]; Rs22 = Result[22];
  //   Rs23 = Result[23]; Rs24 = Result[24]; Rs25 = Result[25]; Rs26 = Result[26]; Rs27 = Result[27];
  //   Rs28 = Result[28]; Rs29 = Result[29]; Rs30 = Result[30]; Rs31 = Result[31]

  // Notes on the sheet:
  //   unsigned
  //   signed
  //   set
  //   signed
  //   unsigned
  //   seteq
  //   old_rd
  //   sset
  //   RD
endmodule
