// Logisim project Fetch_instruction.circ as structural Verilog: 1 circuit, main circuit main
module main (
  input  [31:0] in_1,
  output [5:0] out_2,
  output [4:0] out_3,
  output [4:0] out_4,
  output [4:0] out_5,
  output [10:0] out_6,
  output [15:0] out_7
);


  assign out_2 = in_1[5:0];
  assign out_3 = in_1[10:6];
  assign out_4 = in_1[15:11];
  assign out_5 = in_1[20:16];
  assign out_6 = in_1[31:21];
  assign out_7 = in_1[31:16];

  // Other names for the same wires on the sheet: OP[5:0] = in_1[5:0]; ImmL[4:0] = in_1[10:6]; Rd[4:0] = in_1[10:6];
  //   Rs1[4:0] = in_1[15:11]; Imm16[15:0] = in_1[31:16]; Rs2[4:0] = in_1[20:16]; Funct[10:0] = in_1[31:21];
  //   ImmU[10:0] = in_1[31:21]

  // Notes on the sheet:
  //   Decoding_Instruction
  //   instruction
endmodule
