// Logisim project ForwardUnit1.circ as structural Verilog: 1 circuit, main circuit main
module main (
  input  [4:0] Rs1_EX,
  input  [4:0] Rs1_ID,
  input  MemRead_MEM,
  input  RegWrite_MEM,
  input  RegWrite_WB,
  input  check_is_branch_or_not,
  input  MemRead_EX,
  input  RegWrite_EX,
  input  [4:0] Reg_Des_WB,
  input  [4:0] Rs2_EX,
  input  [4:0] Rs2_ID,
  input  [4:0] Reg_Des_MEM,
  input  [4:0] Reg_Des_EX,
  output [1:0] Forward_A,
  output [1:0] Forward_C,
  output [1:0] Forward_B,
  output [1:0] Forward_D
);

  wire and_1_out, and_2_out, and_3_out, and_4_out, and_5_out, and_6_out, and_7_out, and_8_out, and_9_out,
       and_10_out, and_11_out, and_12_out, comparator_1_eq, comparator_2_eq, comparator_3_eq,
       comparator_4_eq, comparator_5_eq, comparator_6_eq, comparator_7_eq, comparator_8_eq, comparator_9_eq,
       comparator_10_eq, comparator_11_eq, comparator_12_eq, comparator_13_eq, comparator_14_eq,
       comparator_15_eq, comparator_16_eq, Rs1_not_Zero, Rs2_not_Zero;

  Comparator #(.width(5), .mode("unsigned")) comparator_1 (
    .a(Rs1_EX), .b(Reg_Des_MEM), .eq(comparator_1_eq));  // open: gt, lt
  Comparator #(.width(5), .mode("unsigned")) comparator_2 (
    .a(Rs1_EX), .b(Reg_Des_WB), .eq(comparator_2_eq));  // open: gt, lt
  Comparator #(.width(5), .mode("unsigned")) comparator_3 (
    .a(Rs1_EX), .b(Reg_Des_MEM), .eq(comparator_3_eq));  // open: gt, lt
  Comparator #(.width(5), .mode("unsigned")) comparator_4 (
    .a(Rs2_EX), .b(Reg_Des_MEM), .eq(comparator_4_eq));  // open: gt, lt
  Comparator #(.width(5), .mode("unsigned")) comparator_5 (
    .a(Rs2_EX), .b(Reg_Des_WB), .eq(comparator_5_eq));  // open: gt, lt
  Comparator #(.width(5), .mode("unsigned")) comparator_6 (
    .a(Rs2_EX), .b(Reg_Des_MEM), .eq(comparator_6_eq));  // open: gt, lt
  and and_1 (and_1_out, RegWrite_MEM, comparator_1_eq, Rs1_not_Zero);
  and and_2 (and_2_out, ~and_1_out, RegWrite_WB, comparator_2_eq, Rs1_not_Zero);  // AND_Gate
  and and_3 (and_3_out, ~and_1_out, ~and_2_out, MemRead_MEM, RegWrite_MEM, comparator_3_eq, Rs1_not_Zero);  // AND_Gate
  and and_4 (and_4_out, RegWrite_MEM, comparator_4_eq, Rs2_not_Zero);
  and and_5 (and_5_out, ~and_4_out, RegWrite_WB, comparator_5_eq, Rs2_not_Zero);  // AND_Gate
  and and_6 (and_6_out, ~and_4_out, ~and_5_out, MemRead_MEM, RegWrite_MEM, comparator_6_eq, Rs2_not_Zero);  // AND_Gate
  or or_1 (Forward_A[0], and_1_out, and_2_out);
  or or_2 (Forward_A[1], and_2_out, and_3_out);
  or or_3 (Forward_B[0], and_4_out, and_5_out);
  or or_4 (Forward_B[1], and_5_out, and_6_out);
  Comparator #(.width(5), .mode("unsigned")) comparator_7 (
    .a(Rs1_EX), .b({5{1'b0}}), .eq(comparator_7_eq));  // open: gt, lt
  Comparator #(.width(5), .mode("unsigned")) comparator_8 (
    .a(Rs2_EX), .b({5{1'b0}}), .eq(comparator_8_eq));  // open: gt, lt
  not not_1 (Rs1_not_Zero, comparator_7_eq);
  not not_2 (Rs2_not_Zero, comparator_8_eq);
  Comparator #(.width(5), .mode("unsigned")) comparator_9 (
    .a(Rs1_ID), .b(Reg_Des_EX), .eq(comparator_9_eq));  // open: gt, lt
  Comparator #(.width(5), .mode("unsigned")) comparator_10 (
    .a(Rs1_ID), .b(Reg_Des_MEM), .eq(comparator_10_eq));  // open: gt, lt
  Comparator #(.width(5), .mode("unsigned")) comparator_11 (
    .a(Rs1_ID), .b(Reg_Des_EX), .eq(comparator_11_eq));  // open: gt, lt
  Comparator #(.width(5), .mode("unsigned")) comparator_12 (
    .a(Rs2_ID), .b(Reg_Des_EX), .eq(comparator_12_eq));  // open: gt, lt
  Comparator #(.width(5), .mode("unsigned")) comparator_13 (
    .a(Rs2_ID), .b(Reg_Des_MEM), .eq(comparator_13_eq));  // open: gt, lt
  Comparator #(.width(5), .mode("unsigned")) comparator_14 (
    .a(Rs2_ID), .b(Reg_Des_EX), .eq(comparator_14_eq));  // open: gt, lt
  and and_7 (and_7_out, RegWrite_EX, comparator_9_eq, Rs1_not_Zero, check_is_branch_or_not);
  and and_8 (and_8_out, ~and_7_out, RegWrite_MEM, comparator_10_eq, Rs1_not_Zero, check_is_branch_or_not);  // AND_Gate
  and and_9 (and_9_out, ~and_7_out, ~and_8_out, MemRead_EX, RegWrite_EX, comparator_11_eq, Rs1_not_Zero, check_is_branch_or_not);  // AND_Gate
  and and_10 (and_10_out, RegWrite_EX, comparator_12_eq, Rs2_not_Zero, check_is_branch_or_not);
  and and_11 (and_11_out, ~and_10_out, RegWrite_MEM, comparator_13_eq, Rs2_not_Zero, check_is_branch_or_not);  // AND_Gate
  and and_12 (and_12_out, ~and_10_out, ~and_11_out, MemRead_EX, RegWrite_EX, comparator_14_eq, Rs2_not_Zero, check_is_branch_or_not);  // AND_Gate
  or or_5 (Forward_C[0], and_7_out, and_8_out);
  or or_6 (Forward_C[1], and_8_out, and_9_out);
  or or_7 (Forward_D[0], and_10_out, and_11_out);
  or or_8 (Forward_D[1], and_11_out, and_12_out);
  Comparator #(.width(5), .mode("unsigned")) comparator_15 (
    .a(Rs1_ID), .b({5{1'b0}}), .eq(comparator_15_eq));  // open: gt, lt
  Comparator #(.width(5), .mode("unsigned")) comparator_16 (
    .a(Rs2_ID), .b({5{1'b0}}), .eq(comparator_16_eq));  // open: gt, lt
  not not_3 (Rs1_not_Zero, comparator_15_eq);
  not not_4 (Rs2_not_Zero, comparator_16_eq);

  // Other names for the same wires on the sheet: Branch = check_is_branch_or_not

  // Notes on the sheet:
  //   LW
  //   LW
  //   previous
  //   2nd previos
  //   previous
  //   2nd previos
  //   LW
  //   previous
  //   2nd previos
  //   LW
  //   previous
  //   2nd previos
endmodule
