// Logisim project HazardDetection.circ as structural Verilog: 1 circuit, main circuit main
module main (
  input  MemRead_EX,
  input  [4:0] RS1_ID,
  input  [4:0] RD_EX,
  input  [4:0] RS2_ID,
  input  reg_Write_WB,
  input  [4:0] RD_WB,
  input  Branch,
  input  jalr,
  output Stall,
  output Kill
);

  wire and_1_out, and_2_out, and_3_out, comparator_1_eq, comparator_2_eq, comparator_3_eq, comparator_4_eq,
       comparator_5_eq, comparator_6_eq, not_1_out, not_2_out, or_1_out, or_2_out, or_4_out;

  Comparator #(.width(5)) comparator_1 (.a(RS1_ID), .b(RD_EX), .eq(comparator_1_eq));  // open: gt, lt
  Comparator #(.width(5)) comparator_2 (.a(RS2_ID), .b(RD_EX), .eq(comparator_2_eq));  // open: gt, lt
  Comparator #(.width(5)) comparator_3 (.a(RS1_ID), .b(RD_WB), .eq(comparator_3_eq));  // open: gt, lt
  Comparator #(.width(5)) comparator_4 (.a(RS2_ID), .b(RD_WB), .eq(comparator_4_eq));  // open: gt, lt
  or or_1 (or_1_out, comparator_3_eq, comparator_4_eq);
  Comparator #(.width(5)) comparator_5 (.a({5{1'b0}}), .b(RS2_ID), .eq(comparator_5_eq));  // open: gt, lt
  not not_1 (not_1_out, comparator_6_eq);
  Comparator #(.width(5)) comparator_6 (.a({5{1'b0}}), .b(RS1_ID), .eq(comparator_6_eq));  // open: gt, lt
  or or_2 (or_2_out, comparator_1_eq, comparator_2_eq);
  or or_3 (Kill, Branch, jalr);
  not not_2 (not_2_out, comparator_5_eq);
  and and_1 (and_1_out, not_2_out, not_1_out);
  and and_2 (and_2_out, MemRead_EX, or_2_out);
  and and_3 (and_3_out, reg_Write_WB, or_1_out);
  or or_4 (or_4_out, and_2_out, and_3_out);
  and and_4 (Stall, and_1_out, or_4_out);

  // Notes on the sheet:
  //   READ IN 1 CYCLE AND WRITE IN ANOTHER
endmodule
