// Logisim project ID_EX_Reg.circ as structural Verilog: 1 circuit, main circuit main
module main (
  input  [19:0] PC_Inc,
  input  [4:0] RS1,
  input  [4:0] RS2,
  input  [4:0] RD,
  input  [31:0] BusA,
  input  [31:0] BusB,
  input  in_7,
  input  RegWrite,
  input  [15:0] Imm16,
  input  [4:0] ImmL,
  input  [10:0] ImmU,
  input  ExtOp,
  input  [1:0] ALUSrc,
  input  [7:0] ALUOp,
  input  MemRead,
  input  MemWrite,
  input  MemToReg,
  input  jalr,
  input  Sset,
  output [19:0] out_20,
  output [4:0] out_21,
  output [4:0] out_22,
  output [4:0] out_23,
  output [31:0] out_24,
  output [31:0] out_25,
  output out_26,
  output [15:0] out_27,
  output [4:0] out_28,
  output [10:0] out_29,
  output out_30,
  output [1:0] out_31,
  output [7:0] out_32,
  output out_33,
  output out_34,
  output out_35,
  output out_36,
  output out_37
);

  Register #(.width(20)) register_1 (.D(PC_Inc), .en(1'b1), .clk(in_7), .Q(out_20));  // open: clr
  Register #(.width(5)) register_2 (.D(RS1), .en(1'b1), .clk(in_7), .Q(out_21));  // open: clr
  Register #(.width(5)) register_3 (.D(RS2), .en(1'b1), .clk(in_7), .Q(out_22));  // open: clr
  Register #(.width(5)) register_4 (.D(RD), .en(1'b1), .clk(in_7), .Q(out_23));  // open: clr
  Register #(.width(32)) register_5 (.D(BusA), .en(1'b1), .clk(in_7), .Q(out_24));  // open: clr
  Register #(.width(32)) register_6 (.D(BusB), .en(1'b1), .clk(in_7), .Q(out_25));  // open: clr
  Register #(.width(1)) register_7 (.D(RegWrite), .en(1'b1), .clk(in_7), .Q(out_26));  // open: clr
  Register #(.width(16)) register_8 (.D(Imm16), .en(1'b1), .clk(in_7), .Q(out_27));  // open: clr
  Register #(.width(5)) register_9 (.D(ImmL), .en(1'b1), .clk(in_7), .Q(out_28));  // open: clr
  Register #(.width(11)) register_10 (.D(ImmU), .en(1'b1), .clk(in_7), .Q(out_29));  // open: clr
  Register #(.width(1)) register_11 (.D(ExtOp), .en(1'b1), .clk(in_7), .Q(out_30));  // open: clr
  Register #(.width(2)) register_12 (.D(ALUSrc), .en(1'b1), .clk(in_7), .Q(out_31));  // open: clr
  Register register_13 (.D(ALUOp), .en(1'b1), .clk(in_7), .Q(out_32));  // open: clr
  Register #(.width(1)) register_14 (.D(MemRead), .en(1'b1), .clk(in_7), .Q(out_33));  // open: clr
  Register #(.width(1)) register_15 (.D(MemWrite), .en(1'b1), .clk(in_7), .Q(out_34));  // open: clr
  Register #(.width(1)) register_16 (.D(MemToReg), .en(1'b1), .clk(in_7), .Q(out_35));  // open: clr
  Register #(.width(1)) register_17 (.D(jalr), .en(1'b1), .clk(in_7), .Q(out_36));  // open: clr
  Register #(.width(1)) register_18 (.D(Sset), .en(1'b1), .clk(in_7), .Q(out_37));  // open: clr

  // Other names for the same wires on the sheet: CLK = in_7
endmodule
