// Logisim project IF_ID_REGISTER.circ as structural Verilog: 1 circuit, main circuit main
module main (
  input  [31:0] instruction,
  input  [19:0] PC_IF,
  input  [19:0] pc_inc,
  input  kill,
  input  clk,
  input  stall,
  output [31:0] instruction_2,
  output [19:0] PC_ID,
  output [19:0] pc_inc_2,
  output kill_2
);

  wire not_1_out;

  not not_1 (not_1_out, stall);
  Register #(.width(32)) register_1 (.D(instruction), .en(not_1_out), .clk(clk), .Q(instruction_2));  // open: clr
  Register #(.width(20)) register_2 (.D(PC_IF), .en(not_1_out), .clk(clk), .Q(PC_ID));  // open: clr
  Register #(.width(20)) register_3 (.D(pc_inc), .en(not_1_out), .clk(clk), .Q(pc_inc_2));  // open: clr
  Register #(.width(1)) register_4 (.D(kill), .en(not_1_out), .clk(clk), .Q(kill_2));  // open: clr
endmodule
