// Logisim project MEM_WB_Register.circ as structural Verilog: 1 circuit, main circuit main
module main (
  input  in_1,
  input  [31:0] ALU_result_MEM,
  input  RegWrite_MEM,
  input  [4:0] Reg_Des_MEM,
  input  [31:0] MEM_Data_MEM,
  input  MemtoReg_MEM,
  input  [19:0] pc_inc_MEM,
  input  jalr_MEM,
  output RegWrite_WB,
  output [31:0] ALU_result_WB,
  output [4:0] Reg_Des_WB,
  output [31:0] MEM_Data_WB,
  output MemtoReg_WB,
  output [19:0] pc_inc_WB,
  output jalr_WB
);

  Register #(.width(32)) register_1 (.D(ALU_result_MEM), .en(1'b1), .clk(in_1), .Q(ALU_result_WB));  // open: clr
  Register #(.width(32)) register_2 (.D(MEM_Data_MEM), .en(1'b1), .clk(in_1), .Q(MEM_Data_WB));  // open: clr
  Register #(.width(1)) register_3 (.D(MemtoReg_MEM), .en(1'b1), .clk(in_1), .Q(MemtoReg_WB));  // open: clr
  Register #(.width(1)) register_4 (.D(jalr_MEM), .en(1'b1), .clk(in_1), .Q(jalr_WB));  // open: clr
  Register #(.width(20)) register_5 (.D(pc_inc_MEM), .en(1'b1), .clk(in_1), .Q(pc_inc_WB));  // open: clr
  Register #(.width(1)) register_6 (.D(RegWrite_MEM), .en(1'b1), .clk(in_1), .Q(RegWrite_WB));  // open: clr
  Register #(.width(5)) register_7 (.D(Reg_Des_MEM), .en(1'b1), .clk(in_1), .Q(Reg_Des_WB));  // open: clr

  // Other names for the same wires on the sheet: CLK = in_1
endmodule
