// Logisim project MainControlUnit.circ as structural Verilog: 1 circuit, main circuit main
module main (
  input  [10:0] in_1,
  input  [5:0] in_2,
  input  ZeroFlag,
  input  LessFlagSigned,
  input  LessFlagUnsigned,
  output mem_to_reg,
  output Memory_Read,
  output Memory_Write,
  output RegWrite,
  output Extop,
  output [1:0] ALUsrc,
  output [7:0] ALU_Op,
  output branch,
  output SSET,
  output Pc_src,
  output jalr
);

  wire ADD, ADDI, AND, and_1_out, and_2_out, and_3_out, and_4_out, and_5_out, and_6_out, ANDI, BEQ, BGE,
       BGEU, BLT, BLTU, BNE, decoder_1_out0, MUL, NOR, NORI, OR, or_3_out, or_4_out, ORI, ROR, RORI, SEQ,
       SEQI, SET, SLL, SLLI, SLT, SLTI, SLTIU, SLTU, SRA, SRAI, SRL, SRLI, SUB, XOR, XORI;

  or Bit_7 (ALU_Op[7], NOR, NORI);
  or Bit_6 (ALU_Op[6], SUB, NOR, NORI, BEQ, BNE);
  or Bit_0 (ALU_Op[0], SLL, SRA, SLTU, SEQ, SLLI, SRAI, SLTIU, SEQI, SSET, BLTU, BGEU);
  or bit_1 (ALU_Op[1], SRL, SRA, SEQ, SRLI, SLTI, SRAI, MUL, SEQI, BLT, BGE, SLT);
  and and_1 (and_1_out, BEQ, ZeroFlag);
  and and_2 (and_2_out, ~ZeroFlag, BNE);  // AND_Gate
  and and_3 (and_3_out, BLT, LessFlagSigned);
  and and_4 (and_4_out, ~LessFlagSigned, BGE);  // AND_Gate
  and and_5 (and_5_out, BLTU, LessFlagUnsigned);
  and and_6 (and_6_out, ~LessFlagUnsigned, BGEU);  // AND_Gate
  or Bit_5 (ALU_Op[5], ADD, SUB, XOR, ADDI, XORI, mem_to_reg, ALUsrc[1], BEQ, BNE);
  or Bit2 (ALU_Op[2], ROR, SLT, SLTU, SEQ, RORI, SLTI, SLTIU, SEQI, BLT, BGE, BLTU, BGEU);
  or Bit_4 (ALU_Op[4], ADD, SUB, OR, ADDI, ORI, mem_to_reg, ALUsrc[1], BEQ, BNE);
  or Bit_3 (ALU_Op[3], SET, MUL, SSET);
  or or_1 (Pc_src, and_1_out, and_2_out, and_3_out, and_4_out, and_5_out, and_6_out);
  Decoder #(.select(5), .enable("false")) decoder_1 (
    .out0(decoder_1_out0), .out1(SLLI), .out2(SRLI), .out3(SRAI), .out4(RORI), .out5(ADDI), .out6(SLTI),
    .out7(SLTIU), .out8(SEQI), .out9(XORI), .out10(ORI), .out11(ANDI), .out12(NORI), .out13(SET),
    .out14(SSET), .out15(jalr), .out16(mem_to_reg), .out17(ALUsrc[1]), .out18(BEQ), .out19(BNE), .out20(BLT),
    .out21(BGE), .out22(BLTU), .out23(BGEU), .sel(in_2[4:0]));  // open: out24, out25, out26, out27, out28, out29, out30, out31
  Decoder #(.select(4)) decoder_2 (
    .out0(SLL), .out1(SRL), .out2(SRA), .out3(ROR), .out4(ADD), .out5(SUB), .out6(SLT), .out7(SLTU),
    .out8(SEQ), .out9(XOR), .out10(OR), .out11(AND), .out12(NOR), .out13(MUL), .sel(in_1[3:0]),
    .en(decoder_1_out0));  // open: out14, out15
  or or_2 (branch, BEQ, BNE, BLT, BGE, BLTU, BGEU);
  or or_3 (or_3_out, ALUsrc[1], BEQ, BNE, BLT, BGE, BLTU, BGEU);
  or or_4 (or_4_out, SLTIU, XORI, NORI, ORI, ANDI);
  or or_5 (ALUsrc[0], SLLI, SRLI, SRAI, RORI, ADDI, SLTI, SLTIU, SEQI, XORI, ORI, ANDI, NORI, SET, SSET, jalr, mem_to_reg);
  not not_1 (RegWrite, or_3_out);
  not not_2 (Extop, or_4_out);

  assign Memory_Read = mem_to_reg;
  assign Memory_Write = ALUsrc[1];

  // Other names for the same wires on the sheet: SW = ALUsrc[1]; LW = mem_to_reg

  // Notes on the sheet:
  //   JALR
  //   ALU Control
  //   PC Control
  //   ALU_Op
  //   Decoding Instructions
  //   Op=0
  //   Extender
  //   Memory Signals
  //   Reg_Write_Signal
  //   ALUSrc_Signal
  //   SSET_Signal
endmodule
