// Logisim project OpCodeDecoder.circ as structural Verilog: 1 circuit, main circuit main
module main (
  input  [10:0] in_1,
  input  [5:0] in_2,
  output mem_to_reg,
  output Memory_Read,
  output Memory_Write,
  output RegWrite,
  output Extop,
  output [1:0] ALUsrc,
  output SSET
);

  wire ADD, ADDI, AND, ANDI, BEQ, BGE, BGEU, BLT, BLTU, BNE, decoder_1_out0, JALR, MUL, NOR, NORI, OR,
       or_1_out, ORI, ROR, RORI, SEQ, SEQI, SET, SLL, SLLI, SLT, SLTI, SLTIU, SLTU, SRA, SRAI, SRL, SRLI,
       SUB, XOR, XORI;

  Decoder #(.select(5), .enable("false")) decoder_1 (
    .out0(decoder_1_out0), .out1(SLLI), .out2(SRLI), .out3(SRAI), .out4(RORI), .out5(ADDI), .out6(SLTI),
    .out7(SLTIU), .out8(SEQI), .out9(XORI), .out10(ORI), .out11(ANDI), .out12(NORI), .out13(SET),
    .out14(SSET), .out15(JALR), .out16(mem_to_reg), .out17(ALUsrc[1]), .out18(BEQ), .out19(BNE), .out20(BLT),
    .out21(BGE), .out22(BLTU), .out23(BGEU), .sel(in_2[4:0]));  // open: out24, out25, out26, out27, out28, out29, out30, out31
  Decoder #(.select(4)) decoder_2 (
    .out0(SLL), .out1(SRL), .out2(SRA), .out3(ROR), .out4(ADD), .out5(SUB), .out6(SLT), .out7(SLTU),
    .out8(SEQ), .out9(XOR), .out10(OR), .out11(AND), .out12(NOR), .out13(MUL), .sel(in_1[3:0]),
    .en(decoder_1_out0));  // open: out14, out15
  or or_1 (or_1_out, ALUsrc[1], BEQ, BNE, BLT, BGE, BLTU, BGEU);
  or or_2 (Extop, SLTIU, XORI, NORI, ORI, ANDI);
  or or_3 (ALUsrc[0], SLLI, SRLI, SRAI, RORI, ADDI, SLTI, SLTIU, SEQI, XORI, ORI, ANDI, NORI, SET, SSET, JALR, mem_to_reg);
  not not_1 (RegWrite, or_1_out);

  assign Memory_Read = mem_to_reg;
  assign Memory_Write = ALUsrc[1];

  // Other names for the same wires on the sheet: SW = ALUsrc[1]; LW = mem_to_reg

  // Notes on the sheet:
  //   Decoding_Instructions
  //   Op=0
  //   Reg_Write_Signal
  //   Extender
  //   ALUSrc_Signal
  //   Memory Signals
  //   SSET_Signal
endmodule
