// Logisim project RF Akram.circ as structural Verilog: 1 circuit, main circuit main
module main (
  input  [31:0] in_1,
  input  in_2,
  input  [4:0] in_3,
  input  [4:0] in_4,
  input  [4:0] in_5,
  input  clock,
  input  [31:0] Data_Write,
  input  Reg_Write,
  output [31:0] Read_Data_2,
  output [31:0] Read_Data_1
);

  wire and_1_out, and_2_out, and_3_out, and_4_out, and_5_out, and_6_out, and_7_out, and_8_out, and_9_out,
       and_10_out, and_11_out, and_12_out, and_13_out, and_14_out, and_15_out, and_16_out, and_17_out,
       and_18_out, and_19_out, and_20_out, and_21_out, and_22_out, and_23_out, and_24_out, and_25_out,
       and_26_out, and_27_out, and_28_out, and_29_out, and_30_out, and_31_out, and_32_out, decoder_1_out0,
       decoder_1_out1, decoder_1_out2, decoder_1_out3, decoder_1_out4, decoder_1_out5, decoder_1_out6,
       decoder_1_out7, decoder_1_out8, decoder_1_out9, decoder_1_out10, decoder_1_out11, decoder_1_out12,
       decoder_1_out13, decoder_1_out14, decoder_1_out15, decoder_1_out16, decoder_1_out17, decoder_1_out18,
       decoder_1_out19, decoder_1_out20, decoder_1_out21, decoder_1_out22, decoder_1_out23, decoder_1_out24,
       decoder_1_out25, decoder_1_out26, decoder_1_out27, decoder_1_out28, decoder_1_out29, decoder_1_out30,
       decoder_1_out31;
  wire [31:0] R0_q, R1_q, R2_q, R3_q, R4_q, R5_q, R6_q, R7_q, R8_q, R9_q, R10_q, R11_q, R12_q, R13_q, R14_q,
       R15_q, R16_q, R17_q, R18_q, R19_q, R20_q, R21_q, R22_q, R23_q, R24_q, R25_q, R26_q, R27_q, R28_q,
       R29_q, R30_q, R31_q;

  Decoder #(.select(5)) decoder_1 (
    .out0(decoder_1_out0), .out1(decoder_1_out1), .out2(decoder_1_out2), .out3(decoder_1_out3),
    .out4(decoder_1_out4), .out5(decoder_1_out5), .out6(decoder_1_out6), .out7(decoder_1_out7),
    .out8(decoder_1_out8), .out9(decoder_1_out9), .out10(decoder_1_out10), .out11(decoder_1_out11),
    .out12(decoder_1_out12), .out13(decoder_1_out13), .out14(decoder_1_out14), .out15(decoder_1_out15),
    .out16(decoder_1_out16), .out17(decoder_1_out17), .out18(decoder_1_out18), .out19(decoder_1_out19),
    .out20(decoder_1_out20), .out21(decoder_1_out21), .out22(decoder_1_out22), .out23(decoder_1_out23),
    .out24(decoder_1_out24), .out25(decoder_1_out25), .out26(decoder_1_out26), .out27(decoder_1_out27),
    .out28(decoder_1_out28), .out29(decoder_1_out29), .out30(decoder_1_out30), .out31(decoder_1_out31),
    .sel(in_3), .en(in_2));
  and and_1 (and_1_out, decoder_1_out0, Reg_Write);
  and and_2 (and_2_out, decoder_1_out1, Reg_Write);
  and and_3 (and_3_out, decoder_1_out2, Reg_Write);
  and and_4 (and_4_out, decoder_1_out3, Reg_Write);
  and and_5 (and_5_out, decoder_1_out4, Reg_Write);
  and and_6 (and_6_out, decoder_1_out5, Reg_Write);
  and and_7 (and_7_out, decoder_1_out6, Reg_Write);
  and and_8 (and_8_out, decoder_1_out7, Reg_Write);
  and and_9 (and_9_out, decoder_1_out8, Reg_Write);
  and and_10 (and_10_out, decoder_1_out9, Reg_Write);
  and and_11 (and_11_out, decoder_1_out10, Reg_Write);
  and and_12 (and_12_out, decoder_1_out11, Reg_Write);
  and and_13 (and_13_out, decoder_1_out12, Reg_Write);
  and and_14 (and_14_out, decoder_1_out13, Reg_Write);
  and and_15 (and_15_out, decoder_1_out14, Reg_Write);
  and and_16 (and_16_out, decoder_1_out15, Reg_Write);
  and and_17 (and_17_out, decoder_1_out16, Reg_Write);
  and and_18 (and_18_out, decoder_1_out17, Reg_Write);
  and and_19 (and_19_out, decoder_1_out18, Reg_Write);
  and and_20 (and_20_out, decoder_1_out19, Reg_Write);
  and and_21 (and_21_out, decoder_1_out20, Reg_Write);
  and and_22 (and_22_out, decoder_1_out21, Reg_Write);
  and and_23 (and_23_out, decoder_1_out22, Reg_Write);
  and and_24 (and_24_out, decoder_1_out23, Reg_Write);
  and and_25 (and_25_out, decoder_1_out24, Reg_Write);
  and and_26 (and_26_out, decoder_1_out25, Reg_Write);
  and and_27 (and_27_out, decoder_1_out26, Reg_Write);
  and and_28 (and_28_out, decoder_1_out27, Reg_Write);
  and and_29 (and_29_out, decoder_1_out28, Reg_Write);
  and and_30 (and_30_out, decoder_1_out29, Reg_Write);
  and and_31 (and_31_out, decoder_1_out30, Reg_Write);
  and and_32 (and_32_out, decoder_1_out31, Reg_Write);
  Register #(.width(32)) R0 (.D(in_1), .en(and_1_out), .Q(R0_q), .clk(clock));  // open: clr
  Register #(.width(32)) R1 (.D(Data_Write), .en(and_2_out), .Q(R1_q), .clk(clock));  // open: clr
  Register #(.width(32)) R2 (.D(Data_Write), .en(and_3_out), .Q(R2_q), .clk(clock));  // open: clr
  Register #(.width(32)) R3 (.D(Data_Write), .en(and_4_out), .Q(R3_q), .clk(clock));  // open: clr
  Register #(.width(32)) R4 (.D(Data_Write), .en(and_5_out), .Q(R4_q), .clk(clock));  // open: clr
  Register #(.width(32)) R5 (.D(Data_Write), .en(and_6_out), .Q(R5_q), .clk(clock));  // open: clr
  Register #(.width(32)) R6 (.D(Data_Write), .en(and_7_out), .Q(R6_q), .clk(clock));  // open: clr
  Register #(.width(32)) R7 (.D(Data_Write), .en(and_8_out), .Q(R7_q), .clk(clock));  // open: clr
  Register #(.width(32)) R8 (.D(Data_Write), .en(and_9_out), .Q(R8_q), .clk(clock));  // open: clr
  Register #(.width(32)) R9 (.D(Data_Write), .en(and_10_out), .Q(R9_q), .clk(clock));  // open: clr
  Register #(.width(32)) R10 (.D(Data_Write), .en(and_11_out), .Q(R10_q), .clk(clock));  // open: clr
  Register #(.width(32)) R11 (.D(Data_Write), .en(and_12_out), .Q(R11_q), .clk(clock));  // open: clr
  Register #(.width(32)) R12 (.D(Data_Write), .en(and_13_out), .Q(R12_q), .clk(clock));  // open: clr
  Register #(.width(32)) R13 (.D(Data_Write), .en(and_14_out), .Q(R13_q), .clk(clock));  // open: clr
  Register #(.width(32)) R14 (.D(Data_Write), .en(and_15_out), .Q(R14_q), .clk(clock));  // open: clr
  Register #(.width(32)) R15 (.D(Data_Write), .en(and_16_out), .Q(R15_q), .clk(clock));  // open: clr
  Register #(.width(32)) R16 (.D(Data_Write), .en(and_17_out), .Q(R16_q), .clk(clock));  // open: clr
  Register #(.width(32)) R17 (.D(Data_Write), .en(and_18_out), .Q(R17_q), .clk(clock));  // open: clr
  Register #(.width(32)) R18 (.D(Data_Write), .en(and_19_out), .Q(R18_q), .clk(clock));  // open: clr
  Register #(.width(32)) R19 (.D(Data_Write), .en(and_20_out), .Q(R19_q), .clk(clock));  // open: clr
  Register #(.width(32)) R20 (.D(Data_Write), .en(and_21_out), .Q(R20_q), .clk(clock));  // open: clr
  Register #(.width(32)) R21 (.D(Data_Write), .en(and_22_out), .Q(R21_q), .clk(clock));  // open: clr
  Register #(.width(32)) R22 (.D(Data_Write), .en(and_23_out), .Q(R22_q), .clk(clock));  // open: clr
  Register #(.width(32)) R23 (.D(Data_Write), .en(and_24_out), .Q(R23_q), .clk(clock));  // open: clr
  Register #(.width(32)) R24 (.D(Data_Write), .en(and_25_out), .Q(R24_q), .clk(clock));  // open: clr
  Register #(.width(32)) R25 (.D(Data_Write), .en(and_26_out), .Q(R25_q), .clk(clock));  // open: clr
  Register #(.width(32)) R26 (.D(Data_Write), .en(and_27_out), .Q(R26_q), .clk(clock));  // open: clr
  Register #(.width(32)) R27 (.D(Data_Write), .en(and_28_out), .Q(R27_q), .clk(clock));  // open: clr
  Register #(.width(32)) R28 (.D(Data_Write), .en(and_29_out), .Q(R28_q), .clk(clock));  // open: clr
  Register #(.width(32)) R29 (.D(Data_Write), .en(and_30_out), .Q(R29_q), .clk(clock));  // open: clr
  Register #(.width(32)) R30 (.D(Data_Write), .en(and_31_out), .Q(R30_q), .clk(clock));  // open: clr
  Register #(.width(32)) R31 (.D(Data_Write), .en(and_32_out), .Q(R31_q), .clk(clock));  // open: clr
  // Probe on R2_q
  Multiplexer #(.select(5), .width(32)) multiplexer_1 (
    .in0(R0_q), .in1(R1_q), .in2(R2_q), .in3(R3_q), .in4(R4_q), .in5(R5_q), .in6(R6_q), .in7(R7_q),
    .in8(R8_q), .in9(R9_q), .in10(R10_q), .in11(R11_q), .in12(R12_q), .in13(R13_q), .in14(R14_q),
    .in15(R15_q), .in16(R16_q), .in17(R17_q), .in18(R18_q), .in19(R19_q), .in20(R20_q), .in21(R21_q),
    .in22(R22_q), .in23(R23_q), .in24(R24_q), .in25(R25_q), .in26(R26_q), .in27(R27_q), .in28(R28_q),
    .in29(R29_q), .in30(R30_q), .in31(R31_q), .out(Read_Data_1), .sel(in_4));
  Multiplexer #(.enable("true"), .select(5), .width(32)) multiplexer_2 (
    .in0(R0_q), .in1(R1_q), .in2(R2_q), .in3(R3_q), .in4(R4_q), .in5(R5_q), .in6(R6_q), .in7(R7_q),
    .in8(R8_q), .in9(R9_q), .in10(R10_q), .in11(R11_q), .in12(R12_q), .in13(R13_q), .in14(R14_q),
    .in15(R15_q), .in16(R16_q), .in17(R17_q), .in18(R18_q), .in19(R19_q), .in20(R20_q), .in21(R21_q),
    .in22(R22_q), .in23(R23_q), .in24(R24_q), .in25(R25_q), .in26(R26_q), .in27(R27_q), .in28(R28_q),
    .in29(R29_q), .in30(R30_q), .in31(R31_q), .out(Read_Data_2), .sel(in_5));  // open: en
endmodule
