// Logisim project RF.circ as structural Verilog
module Reg_file (
  input  [31:0] in_1,
  input  [31:0] in_2,
  input  [31:0] in_3,
  input  [31:0] in_4,
  input  [31:0] in_5,
  input  [31:0] in_6,
  input  [31:0] in_7,
  input  [31:0] in_8,
  input  [31:0] in_9,
  input  [31:0] in_10,
  input  [31:0] in_11,
  input  [31:0] in_12,
  input  [31:0] in_13,
  input  [31:0] in_14,
  input  [4:0] in_15,
  input  [31:0] in_16,
  input  [31:0] in_17,
  input  in_18,
  input  [4:0] RW,
  input  [31:0] in_20,
  input  [31:0] in_21,
  input  [31:0] in_22,
  input  [31:0] in_23,
  input  [31:0] in_24,
  input  [31:0] in_25,
  input  [31:0] in_26,
  input  [31:0] in_27,
  input  [31:0] in_28,
  input  [4:0] in_29,
  input  [31:0] in_30,
  input  [31:0] in_31,
  input  [31:0] in_32,
  input  [31:0] in_33,
  input  [31:0] in_34,
  input  [31:0] in_35,
  input  [31:0] in_36,
  input  clock,
  input  Reg_Write,
  input  [31:0] DATA_IN,
  output [31:0] out_40,
  output [31:0] out_41
);

  wire and_1_out, and_2_out, and_3_out, and_4_out, and_5_out, and_6_out, and_7_out, and_8_out, and_9_out,
       and_10_out, and_11_out, and_12_out, and_13_out, and_14_out, and_15_out, and_16_out, and_17_out,
       and_18_out, and_19_out, and_20_out, and_21_out, and_22_out, and_23_out, and_24_out, and_25_out,
       and_26_out, and_27_out, and_28_out, and_29_out, and_30_out, and_31_out, and_32_out, decoder_1_out0,
       decoder_1_out1, decoder_1_out2, decoder_1_out3, decoder_1_out4, decoder_1_out5, decoder_1_out6,
       decoder_1_out7, decoder_1_out8, decoder_1_out9, decoder_1_out10, decoder_1_out11, decoder_1_out12,
       decoder_1_out13, decoder_1_out14, decoder_1_out15, decoder_1_out16, decoder_1_out17, decoder_1_out18,
       decoder_1_out19, decoder_1_out20, decoder_1_out21, decoder_1_out22, decoder_1_out23, decoder_1_out24,
       decoder_1_out25, decoder_1_out26, decoder_1_out27, decoder_1_out28, decoder_1_out29, decoder_1_out30,
       decoder_1_out31;

  Decoder #(.select(5)) decoder_1 (
    .out0(decoder_1_out0), .out1(decoder_1_out1), .out2(decoder_1_out2), .out3(decoder_1_out3),
    .out4(decoder_1_out4), .out5(decoder_1_out5), .out6(decoder_1_out6), .out7(decoder_1_out7),
    .out8(decoder_1_out8), .out9(decoder_1_out9), .out10(decoder_1_out10), .out11(decoder_1_out11),
    .out12(decoder_1_out12), .out13(decoder_1_out13), .out14(decoder_1_out14), .out15(decoder_1_out15),
    .out16(decoder_1_out16), .out17(decoder_1_out17), .out18(decoder_1_out18), .out19(decoder_1_out19),
    .out20(decoder_1_out20), .out21(decoder_1_out21), .out22(decoder_1_out22), .out23(decoder_1_out23),
    .out24(decoder_1_out24), .out25(decoder_1_out25), .out26(decoder_1_out26), .out27(decoder_1_out27),
    .out28(decoder_1_out28), .out29(decoder_1_out29), .out30(decoder_1_out30), .out31(decoder_1_out31),
    .sel(RW), .en(in_18));
  and and_1 (and_1_out, decoder_1_out0, Reg_Write);
  and and_2 (and_2_out, decoder_1_out1, Reg_Write);
  and and_3 (and_3_out, decoder_1_out2, Reg_Write);
  and and_4 (and_4_out, decoder_1_out3, Reg_Write);
  and and_5 (and_5_out, decoder_1_out4, Reg_Write);
  and and_6 (and_6_out, decoder_1_out5, Reg_Write);
  and and_7 (and_7_out, decoder_1_out6, Reg_Write);
  and and_8 (and_8_out, decoder_1_out7, Reg_Write);
  and and_9 (and_9_out, decoder_1_out8, Reg_Write);
  and and_10 (and_10_out, decoder_1_out9, Reg_Write);
  and and_11 (and_11_out, decoder_1_out10, Reg_Write);
  and and_12 (and_12_out, decoder_1_out11, Reg_Write);
  and and_13 (and_13_out, decoder_1_out12, Reg_Write);
  and and_14 (and_14_out, decoder_1_out13, Reg_Write);
  and and_15 (and_15_out, decoder_1_out14, Reg_Write);
  and and_16 (and_16_out, decoder_1_out15, Reg_Write);
  and and_17 (and_17_out, decoder_1_out16, Reg_Write);
  and and_18 (and_18_out, decoder_1_out17, Reg_Write);
  and and_19 (and_19_out, decoder_1_out18, Reg_Write);
  and and_20 (and_20_out, decoder_1_out19, Reg_Write);
  and and_21 (and_21_out, decoder_1_out20, Reg_Write);
  and and_22 (and_22_out, decoder_1_out21, Reg_Write);
  and and_23 (and_23_out, decoder_1_out22, Reg_Write);
  and and_24 (and_24_out, decoder_1_out23, Reg_Write);
  and and_25 (and_25_out, decoder_1_out24, Reg_Write);
  and and_26 (and_26_out, decoder_1_out25, Reg_Write);
  and and_27 (and_27_out, decoder_1_out26, Reg_Write);
  and and_28 (and_28_out, decoder_1_out27, Reg_Write);
  and and_29 (and_29_out, decoder_1_out28, Reg_Write);
  and and_30 (and_30_out, decoder_1_out29, Reg_Write);
  and and_31 (and_31_out, decoder_1_out30, Reg_Write);
  and and_32 (and_32_out, decoder_1_out31, Reg_Write);
  Register #(.width(32)) register_1 (.D({32{1'b0}}), .en(and_1_out), .clk(clock), .Q(in_1));  // open: clr
  Register #(.width(32)) register_2 (.D(DATA_IN), .en(and_3_out), .clk(clock), .Q(in_3));  // open: clr
  Register #(.width(32)) register_3 (.D(DATA_IN), .en(and_5_out), .clk(clock), .Q(in_5));  // open: clr
  Register #(.width(32)) register_4 (.D(DATA_IN), .en(and_7_out), .clk(clock), .Q(in_8));  // open: clr
  Register #(.width(32)) register_5 (.D(DATA_IN), .en(and_9_out), .clk(clock), .Q(in_9));  // open: clr
  Register #(.width(32)) register_6 (.D(DATA_IN), .en(and_11_out), .clk(clock), .Q(in_12));  // open: clr
  Register #(.width(32)) register_7 (.D(DATA_IN), .en(and_13_out), .clk(clock), .Q(in_14));  // open: clr
  Register #(.width(32)) register_8 (.D(DATA_IN), .en(and_15_out), .clk(clock), .Q(in_17));  // open: clr
  Register #(.width(32)) register_9 (.D(DATA_IN), .en(and_17_out), .clk(clock), .Q(in_21));  // open: clr
  Register #(.width(32)) register_10 (.D(DATA_IN), .en(and_19_out), .clk(clock), .Q(in_23));  // open: clr
  Register #(.width(32)) register_11 (.D(DATA_IN), .en(and_21_out), .clk(clock), .Q(in_25));  // open: clr
  Register #(.width(32)) register_12 (.D(DATA_IN), .en(and_23_out), .clk(clock), .Q(in_26));  // open: clr
  Register #(.width(32)) register_13 (.D(DATA_IN), .en(and_25_out), .clk(clock), .Q(in_28));  // open: clr
  Register #(.width(32)) register_14 (.D(DATA_IN), .en(and_27_out), .clk(clock), .Q(in_32));  // open: clr
  Register #(.width(32)) register_15 (.D(DATA_IN), .en(and_29_out), .clk(clock), .Q(in_34));  // open: clr
  Register #(.width(32)) register_16 (.D(DATA_IN), .en(and_31_out), .clk(clock), .Q(in_36), .clr(and_32_out));
  Register #(.width(32)) register_17 (.D(DATA_IN), .en(and_2_out), .clk(clock), .Q(in_2));  // open: clr
  Register #(.width(32)) register_18 (.D(DATA_IN), .en(and_4_out), .clk(clock), .Q(in_4));  // open: clr
  Register #(.width(32)) register_19 (.D(DATA_IN), .en(and_6_out), .clk(clock), .Q(in_6));  // open: clr
  Register #(.width(32)) register_20 (.D(DATA_IN), .en(and_8_out), .clk(clock), .Q(in_7));  // open: clr
  Register #(.width(32)) register_21 (.D(DATA_IN), .en(and_10_out), .clk(clock), .Q(in_10));  // open: clr
  Register #(.width(32)) register_22 (.D(DATA_IN), .en(and_12_out), .clk(clock), .Q(in_11));  // open: clr
  Register #(.width(32)) register_23 (.D(DATA_IN), .en(and_14_out), .clk(clock), .Q(in_13));  // open: clr
  Register #(.width(32)) register_24 (.D(DATA_IN), .en(and_16_out), .clk(clock), .Q(in_16));  // open: clr
  Register #(.width(32)) register_25 (.D(DATA_IN), .en(and_18_out), .clk(clock), .Q(in_20));  // open: clr
  Register #(.width(32)) register_26 (.D(DATA_IN), .en(and_20_out), .clk(clock), .Q(in_22));  // open: clr
  Register #(.width(32)) register_27 (.D(DATA_IN), .en(and_22_out), .clk(clock), .Q(in_24));  // open: clr
  Register #(.width(32)) register_28 (.D(DATA_IN), .en(and_24_out), .clk(clock), .Q(in_27));  // open: clr
  Register #(.width(32)) register_29 (.D(DATA_IN), .en(and_26_out), .clk(clock), .Q(in_30));  // open: clr
  Register #(.width(32)) register_30 (.D(DATA_IN), .en(and_28_out), .clk(clock), .Q(in_31));  // open: clr
  Register #(.width(32)) register_31 (.D(DATA_IN), .en(and_30_out), .clk(clock), .Q(in_33));  // open: clr
  Register #(.width(32)) register_32 (.D(DATA_IN), .en(and_32_out), .clk(clock), .Q(in_35));  // open: clr
  Multiplexer #(.select(5), .width(32)) multiplexer_1 (
    .in0(in_1), .in1(in_2), .in2(in_3), .in3(in_4), .in4(in_5), .in5(in_6), .in6(in_8), .in7(in_7),
    .in8(in_9), .in9(in_10), .in10(in_12), .in11(in_11), .in12(in_14), .in13(in_13), .in14(in_17),
    .in15(in_16), .in16(in_21), .in17(in_20), .in18(in_23), .in19(in_22), .in20(in_25), .in21(in_24),
    .in22(in_26), .in23(in_27), .in24(in_28), .in25(in_30), .in26(in_32), .in27(in_31), .in28(in_34),
    .in29(in_33), .in30(in_36), .in31(in_35), .out(out_41), .sel(in_29));  // open: en
  Multiplexer #(.select(5), .width(32)) multiplexer_2 (
    .in0(in_1), .in1(in_2), .in2(in_3), .in3(in_4), .in4(in_5), .in5(in_6), .in6(in_8), .in7(in_7),
    .in8(in_9), .in9(in_10), .in10(in_12), .in11(in_11), .in12(in_14), .in13(in_13), .in14(in_17),
    .in15(in_16), .in16(in_21), .in17(in_20), .in18(in_23), .in19(in_22), .in20(in_25), .in21(in_24),
    .in22(in_26), .in23(in_27), .in24(in_28), .in25(in_30), .in26(in_32), .in27(in_31), .in28(in_34),
    .in29(in_33), .in30(in_36), .in31(in_35), .out(out_40), .sel(in_15));  // open: en

  // Other names for the same wires on the sheet: R0[31:0] = in_1; R1[31:0] = in_2; R2[31:0] = in_3; R3[31:0] = in_4;
  //   R4[31:0] = in_5; R5[31:0] = in_6; R6[31:0] = in_8; R7[31:0] = in_7; R8[31:0] = in_9; R9[31:0] = in_10;
  //   R10[31:0] = in_12; R11[31:0] = in_11; R12[31:0] = in_14; R13[31:0] = in_13; R14[31:0] = in_17;
  //   R15[31:0] = in_16; R16[31:0] = in_21; R17[31:0] = in_20; R18[31:0] = in_23; R19[31:0] = in_22;
  //   R20[31:0] = in_25; R21[31:0] = in_24; R22[31:0] = in_26; R23[31:0] = in_27; R24[31:0] = in_28;
  //   R25[31:0] = in_30; R26[31:0] = in_32; R27[31:0] = in_31; R28[31:0] = in_34; R29[31:0] = in_33;
  //   R30[31:0] = in_36; R31[31:0] = in_35
endmodule
