// Logisim project instruction_mem.circ as structural Verilog: 1 circuit, main circuit main
module main (
  input  [19:0] in_1,
  output [31:0] out_2
);

  ROM #(.addrWidth(20), .dataWidth(32)) rom_1 (.addr(in_1), .data(out_2));

  // Notes on the sheet:
  //   pc
  //   contents of rom_1 (hex, n*v repeats v):
  //   1004d a008d 128900cd 45ac00ce 500010d 7342010e 384004d 1234020d 5678020e 140945 12508c0 834100 50
  //   10090 200d0 a42100 841100 c31180 30d2 820880 ffe00712 40011 1a31280 245380 4453c0 57684 2501cf
  //   4545024d 4545028d 95095 ffff0dcb 12 1431140 50 50890 608d0 1631100 40011 380f
  //   instruction
endmodule
