// Logisim project instruction_memory.circ as structural Verilog: 1 circuit, main circuit main
module main (
);

  wire [19:0] pc;
  wire [31:0] instruction;

  ROM #(.addrWidth(20), .dataWidth(32)) rom_1 (.addr(pc), .data(instruction));

  // Notes on the sheet:
  //   contents of rom_1 (hex, n*v repeats v):
  //   2222 564511 7776 88765 233 77665 999 5*0 22 0 33 122 657*0 1234 775 33
endmodule
