// Logisim project pc_circut.circ as structural Verilog: 1 circuit, main circuit main
module main (
  input  [10:0] upper11,
  input  [4:0] Lower5,
  input  in_3,
  input  pc_src,
  input  jalr,
  input  [15:0] IMM16,
  input  [31:0] RS1,
  output [19:0] next_pc,
  output [19:0] out_9,
  output [19:0] out_10
);

  wire [19:0] adder_2_out, adder_3_out, bit_extender_1_out, bit_extender_2_out, multiplexer_1_out;

  // Probe on {upper11, Lower5}
  assign bit_extender_1_out = {{4{upper11[10]}}, {upper11, Lower5}};  // Bit_Extender bit_extender_1
  // Probe on out_10
  Register #(.width(20)) register_1 (.D(next_pc), .en(1'b1), .clk(in_3), .Q(out_10));  // open: clr
  assign bit_extender_2_out = {{4{IMM16[15]}}, IMM16};  // Bit_Extender bit_extender_2
  // Probe on out_9
  Adder #(.width(20)) adder_1 (.a(out_10), .b(20'h1), .out(out_9), .cin(1'b0));  // open: cout
  Adder #(.width(20)) adder_2 (.a(bit_extender_1_out), .b(out_10), .out(adder_2_out), .cin(1'b0));  // open: cout
  Adder #(.width(20)) adder_3 (.a(bit_extender_2_out), .b(RS1[19:0]), .out(adder_3_out), .cin(1'b0));  // open: cout
  // Probe on next_pc
  Multiplexer #(.width(20), .enable("false")) multiplexer_1 (
    .in0(out_9), .in1(adder_2_out), .out(multiplexer_1_out), .sel(pc_src));
  Multiplexer #(.width(20), .enable("false")) multiplexer_2 (
    .in0(multiplexer_1_out), .in1(adder_3_out), .out(next_pc), .sel(jalr));

  // Other names for the same wires on the sheet: pc[19:0] = out_10; pc_inc[19:0] = out_9

  // Notes on the sheet:
  //   pc+1
endmodule
