// Logisim project reg_file.circ as structural Verilog
module register_file (
  input  [31:0] in_1,
  input  [4:0] in_2,
  input  in_3,
  input  [4:0] RW,
  input  [4:0] in_5,
  input  clock,
  input  Reg_Write,
  input  [31:0] DATA_IN,
  output [31:0] out_9,
  output [31:0] out_10
);

  wire and_1_out, and_2_out, and_3_out, and_4_out, and_5_out, and_6_out, and_7_out, and_8_out, and_9_out,
       and_10_out, and_11_out, and_12_out, and_13_out, and_14_out, and_15_out, and_16_out, and_17_out,
       and_18_out, and_19_out, and_20_out, and_21_out, and_22_out, and_23_out, and_24_out, and_25_out,
       and_26_out, and_27_out, and_28_out, and_29_out, and_30_out, and_31_out, and_32_out, decoder_1_out0,
       decoder_1_out1, decoder_1_out2, decoder_1_out3, decoder_1_out4, decoder_1_out5, decoder_1_out6,
       decoder_1_out7, decoder_1_out8, decoder_1_out9, decoder_1_out10, decoder_1_out11, decoder_1_out12,
       decoder_1_out13, decoder_1_out14, decoder_1_out15, decoder_1_out16, decoder_1_out17, decoder_1_out18,
       decoder_1_out19, decoder_1_out20, decoder_1_out21, decoder_1_out22, decoder_1_out23, decoder_1_out24,
       decoder_1_out25, decoder_1_out26, decoder_1_out27, decoder_1_out28, decoder_1_out29, decoder_1_out30,
       decoder_1_out31;
  wire [31:0] R1, R2, R3, R4, R5, R6, R7, R8, R9, R10, R11, R12, R13, R14, R15, R16, R17, R18, R19, R20, R21,
       R22, R23, R24, R25, R26, R27, R28, R29, R30, R31;

  Decoder #(.select(5)) decoder_1 (
    .out0(decoder_1_out0), .out1(decoder_1_out1), .out2(decoder_1_out2), .out3(decoder_1_out3),
    .out4(decoder_1_out4), .out5(decoder_1_out5), .out6(decoder_1_out6), .out7(decoder_1_out7),
    .out8(decoder_1_out8), .out9(decoder_1_out9), .out10(decoder_1_out10), .out11(decoder_1_out11),
    .out12(decoder_1_out12), .out13(decoder_1_out13), .out14(decoder_1_out14), .out15(decoder_1_out15),
    .out16(decoder_1_out16), .out17(decoder_1_out17), .out18(decoder_1_out18), .out19(decoder_1_out19),
    .out20(decoder_1_out20), .out21(decoder_1_out21), .out22(decoder_1_out22), .out23(decoder_1_out23),
    .out24(decoder_1_out24), .out25(decoder_1_out25), .out26(decoder_1_out26), .out27(decoder_1_out27),
    .out28(decoder_1_out28), .out29(decoder_1_out29), .out30(decoder_1_out30), .out31(decoder_1_out31),
    .sel(RW), .en(in_3));
  and and_1 (and_1_out, decoder_1_out0, Reg_Write);
  and and_2 (and_2_out, decoder_1_out1, Reg_Write);
  and and_3 (and_3_out, decoder_1_out2, Reg_Write);
  and and_4 (and_4_out, decoder_1_out3, Reg_Write);
  and and_5 (and_5_out, decoder_1_out4, Reg_Write);
  and and_6 (and_6_out, decoder_1_out5, Reg_Write);
  and and_7 (and_7_out, decoder_1_out6, Reg_Write);
  and and_8 (and_8_out, decoder_1_out7, Reg_Write);
  and and_9 (and_9_out, decoder_1_out8, Reg_Write);
  and and_10 (and_10_out, decoder_1_out9, Reg_Write);
  and and_11 (and_11_out, decoder_1_out10, Reg_Write);
  and and_12 (and_12_out, decoder_1_out11, Reg_Write);
  and and_13 (and_13_out, decoder_1_out12, Reg_Write);
  and and_14 (and_14_out, decoder_1_out13, Reg_Write);
  and and_15 (and_15_out, decoder_1_out14, Reg_Write);
  and and_16 (and_16_out, decoder_1_out15, Reg_Write);
  and and_17 (and_17_out, decoder_1_out16, Reg_Write);
  and and_18 (and_18_out, decoder_1_out17, Reg_Write);
  and and_19 (and_19_out, decoder_1_out18, Reg_Write);
  and and_20 (and_20_out, decoder_1_out19, Reg_Write);
  and and_21 (and_21_out, decoder_1_out20, Reg_Write);
  and and_22 (and_22_out, decoder_1_out21, Reg_Write);
  and and_23 (and_23_out, decoder_1_out22, Reg_Write);
  and and_24 (and_24_out, decoder_1_out23, Reg_Write);
  and and_25 (and_25_out, decoder_1_out24, Reg_Write);
  and and_26 (and_26_out, decoder_1_out25, Reg_Write);
  and and_27 (and_27_out, decoder_1_out26, Reg_Write);
  and and_28 (and_28_out, decoder_1_out27, Reg_Write);
  and and_29 (and_29_out, decoder_1_out28, Reg_Write);
  and and_30 (and_30_out, decoder_1_out29, Reg_Write);
  and and_31 (and_31_out, decoder_1_out30, Reg_Write);
  and and_32 (and_32_out, decoder_1_out31, Reg_Write);
  Register #(.width(32)) register_1 (.D(DATA_IN), .en(and_1_out), .clk(clock), .Q(in_1));  // open: clr
  Register #(.width(32)) register_2 (.D(DATA_IN), .en(and_3_out), .clk(clock), .Q(R2));  // open: clr
  Register #(.width(32)) register_3 (.D(DATA_IN), .en(and_5_out), .clk(clock), .Q(R4));  // open: clr
  Register #(.width(32)) register_4 (.D(DATA_IN), .en(and_7_out), .clk(clock), .Q(R6));  // open: clr
  Register #(.width(32)) register_5 (.D(DATA_IN), .en(and_9_out), .clk(clock), .Q(R8));  // open: clr
  Register #(.width(32)) register_6 (.D(DATA_IN), .en(and_11_out), .clk(clock), .Q(R10));  // open: clr
  Register #(.width(32)) register_7 (.D(DATA_IN), .en(and_13_out), .clk(clock), .Q(R12));  // open: clr
  Register #(.width(32)) register_8 (.D(DATA_IN), .en(and_15_out), .clk(clock), .Q(R14));  // open: clr
  Register #(.width(32)) register_9 (.D(DATA_IN), .en(and_17_out), .clk(clock), .Q(R16));  // open: clr
  Register #(.width(32)) register_10 (.D(DATA_IN), .en(and_19_out), .clk(clock), .Q(R18));  // open: clr
  Register #(.width(32)) register_11 (.D(DATA_IN), .en(and_21_out), .clk(clock), .Q(R20));  // open: clr
  Register #(.width(32)) register_12 (.D(DATA_IN), .en(and_23_out), .clk(clock), .Q(R22));  // open: clr
  Register #(.width(32)) register_13 (.D(DATA_IN), .en(and_25_out), .clk(clock), .Q(R24));  // open: clr
  Register #(.width(32)) register_14 (.D(DATA_IN), .en(and_27_out), .clk(clock), .Q(R26));  // open: clr
  Register #(.width(32)) register_15 (.D(DATA_IN), .en(and_29_out), .clk(clock), .Q(R28));  // open: clr
  Register #(.width(32)) register_16 (.D(DATA_IN), .en(and_31_out), .clk(clock), .Q(R30), .clr(and_32_out));
  // Probe on in_1
  // Probe on R2
  // Probe on R4
  // Probe on R6
  // Probe on R8
  // Probe on R10
  // Probe on R12
  // Probe on R14
  // Probe on R16
  // Probe on R18
  // Probe on R20
  // Probe on R22
  // Probe on R24
  // Probe on R26
  // Probe on R28
  // Probe on R30
  Register #(.width(32)) register_17 (.D(DATA_IN), .en(and_2_out), .clk(clock), .Q(R1));  // open: clr
  Register #(.width(32)) register_18 (.D(DATA_IN), .en(and_4_out), .clk(clock), .Q(R3));  // open: clr
  Register #(.width(32)) register_19 (.D(DATA_IN), .en(and_6_out), .clk(clock), .Q(R5));  // open: clr
  Register #(.width(32)) register_20 (.D(DATA_IN), .en(and_8_out), .clk(clock), .Q(R7));  // open: clr
  Register #(.width(32)) register_21 (.D(DATA_IN), .en(and_10_out), .clk(clock), .Q(R9));  // open: clr
  Register #(.width(32)) register_22 (.D(DATA_IN), .en(and_12_out), .clk(clock), .Q(R11));  // open: clr
  Register #(.width(32)) register_23 (.D(DATA_IN), .en(and_14_out), .clk(clock), .Q(R13));  // open: clr
  Register #(.width(32)) register_24 (.D(DATA_IN), .en(and_16_out), .clk(clock), .Q(R15));  // open: clr
  Register #(.width(32)) register_25 (.D(DATA_IN), .en(and_18_out), .clk(clock), .Q(R17));  // open: clr
  Register #(.width(32)) register_26 (.D(DATA_IN), .en(and_20_out), .clk(clock), .Q(R19));  // open: clr
  Register #(.width(32)) register_27 (.D(DATA_IN), .en(and_22_out), .clk(clock), .Q(R21));  // open: clr
  Register #(.width(32)) register_28 (.D(DATA_IN), .en(and_24_out), .clk(clock), .Q(R23));  // open: clr
  Register #(.width(32)) register_29 (.D(DATA_IN), .en(and_26_out), .clk(clock), .Q(R25));  // open: clr
  Register #(.width(32)) register_30 (.D(DATA_IN), .en(and_28_out), .clk(clock), .Q(R27));  // open: clr
  Register #(.width(32)) register_31 (.D(DATA_IN), .en(and_30_out), .clk(clock), .Q(R29));  // open: clr
  Register #(.width(32)) register_32 (.D(DATA_IN), .en(and_32_out), .clk(clock), .Q(R31));  // open: clr
  // Probe on R1
  // Probe on R3
  // Probe on R5
  // Probe on R7
  // Probe on R9
  // Probe on R11
  // Probe on R13
  // Probe on R15
  // Probe on R17
  // Probe on R19
  // Probe on R21
  // Probe on R23
  // Probe on R25
  // Probe on R27
  // Probe on R29
  // Probe on R29
  // Probe on R31
  Multiplexer #(.enable("true"), .select(5), .width(32)) multiplexer_1 (
    .in0(in_1), .in1(R1), .in2(R2), .in3(R3), .in4(R4), .in5(R5), .in6(R6), .in7(R7), .in8(R8), .in9(R9),
    .in10(R10), .in11(R11), .in12(R12), .in13(R13), .in14(R14), .in15(R15), .in16(R16), .in17(R17),
    .in18(R18), .in19(R19), .in20(R20), .in21(R21), .in22(R22), .in23(R23), .in24(R24), .in25(R25),
    .in26(R26), .in27(R27), .in28(R28), .in29(R29), .in30(R30), .in31(R31), .out(out_10), .sel(in_5));  // open: en
  Multiplexer #(.enable("true"), .select(5), .width(32)) multiplexer_2 (
    .in0(in_1), .in1(R1), .in2(R2), .in3(R3), .in4(R4), .in5(R5), .in6(R6), .in7(R7), .in8(R8), .in9(R9),
    .in10(R10), .in11(R11), .in12(R12), .in13(R13), .in14(R14), .in15(R15), .in16(R16), .in17(R17),
    .in18(R18), .in19(R19), .in20(R20), .in21(R21), .in22(R22), .in23(R23), .in24(R24), .in25(R25),
    .in26(R26), .in27(R27), .in28(R28), .in29(R29), .in30(R30), .in31(R31), .out(out_9), .sel(in_2));  // open: en

  // Other names for the same wires on the sheet: R0[31:0] = in_1
endmodule
