// Logisim project SingleCycleCirc.circ as structural Verilog: 1 circuit, main circuit main
module main (
  output [15:0] out_1,
  output [15:0] out_2,
  output [15:0] out_3,
  output [15:0] out_4,
  output [15:0] out_5,
  output [15:0] out_6,
  output [15:0] out_7,
  output [15:0] out_8,
  output Overflow,
  output CarryOut
);

  wire ALUSrc, Clock, LessFlag, MemRd, MemWr, RegWrite, SignOrZeroExtend, ZeroFlag;
  wire [1:0] Fn, MemtoReg, PCSrc, RegDst;
  wire [2:0] Imm5, multiplexer_1_out;
  wire [5:0] Imm11;
  wire [6:0] ALUop;
  wire [15:0] ALUResult, bit_extender_1_out, bit_extender_2_out, bit_extender_3_out, BusA, BusB, BusW,
       multiplexer_2_out, multiplexer_3_out, NextPc, Pc, ram_1_dout, shifter_1_out;
  wire [15:11] Instruction;

  Clock clock_1 (.out(Clock));
  // Probe on RegDst
  // Probe on Imm11[2:0]
  // Probe on multiplexer_1_out
  Multiplexer #(.select(2), .width(3), .enable("false")) multiplexer_1 (
    .in0(Imm11[2:0]), .in1(Imm5), .in2(3'b001), .in3(3'b111), .out(multiplexer_1_out), .sel(RegDst));
  // PC_main main_1: pin names not known; wires that end beside it: {Fn, Imm5}, {Fn, Imm5, Imm11}, BusA, Clock, PCSrc, NextPc, Pc
  // Probe on Pc
  // Probe on BusW
  // RegisterFile_main main_2: pin names not known; wires that end beside it: RegWrite, out_2, out_3, out_4, out_5, out_6, out_7, BusW, out_8, BusA, BusB
  // Probe on BusB
  // Probe on out_1
  // Probe on {Fn, Imm5}
  // Probe on out_2
  assign bit_extender_1_out = {{11{1'b0}}, {Fn, Imm5}};  // Bit_Extender bit_extender_1
  assign bit_extender_2_out = {{11{Fn[1]}}, {Fn, Imm5}};  // Bit_Extender bit_extender_2
  // Probe on Instruction
  // Probe on out_3
  ROM #(.addrWidth(16), .dataWidth(16)) rom_1 (.addr(Pc), .data({Instruction, Fn, Imm5, Imm11}));
  // Probe on BusB
  Multiplexer #(.width(16), .enable("false")) multiplexer_2 (
    .in0(bit_extender_1_out), .in1(bit_extender_2_out), .out(multiplexer_2_out), .sel(SignOrZeroExtend));
  // Probe on BusA
  Multiplexer #(.width(16), .enable("false")) multiplexer_3 (
    .in0(BusB), .in1(multiplexer_2_out), .out(multiplexer_3_out), .sel(ALUSrc));
  // Probe on multiplexer_3_out
  // Probe on multiplexer_2_out
  // Probe on ALUSrc
  // Probe on out_4
  // Probe on out_5
  // Probe on out_6
  // Probe on ALUResult
  // Alu16bit alu16bit_1: pin names not known; wires that end beside it: BusA, multiplexer_3_out, ALUop[5], ALUop[6], ALUop[5], ALUop[4:3], ALUop[2:0], ALUResult, LessFlag, Overflow, CarryOut, ZeroFlag
  // Control_Unit_main main_3: pin names not known; wires that end beside it: RegDst, ALUSrc, MemtoReg, MemWr, MemRd, RegWrite
  // Probe on out_7
  // Probe on out_8
  // Probe on BusB
  RAM #(.addrWidth(16), .dataWidth(16), .trigger("falling"), .databus("bibus")) ram_1 (
    .addr(ALUResult), .we(MemWr), .oe(MemRd), .clk(Clock), .din(BusB), .dout(ram_1_dout));
  // Probe on {Fn, Imm5}
  assign bit_extender_3_out = {{5{1'b0}}, {Fn, Imm5, Imm11}};  // Bit_Extender bit_extender_3
  Shifter #(.width(16)) shifter_1 (.in(bit_extender_3_out), .\dist (4'b0101), .out(shifter_1_out));
  Multiplexer #(.select(2), .width(16), .enable("false")) multiplexer_4 (
    .in0(ALUResult), .in1(ram_1_dout), .in2(shifter_1_out), .in3(NextPc), .out(BusW), .sel(MemtoReg));
  // Probe on MemtoReg

  // Other names for the same wires on the sheet: Instruction[10:0] = {Fn, Imm5, Imm11}; Rt[2:0] = Imm11[2:0];
  //   Rs[2:0] = Imm11[5:3]; Imm11[10:6] = {Fn, Imm5}; Rd[2:0] = Imm5; Imm5[4:3] = Fn; Op[4:0] = Instruction;
  //   R0[15:0] = out_1; R1[15:0] = out_2; R2[15:0] = out_3; R3[15:0] = out_4; R4[15:0] = out_5; R5[15:0] = out_6;
  //   R6[15:0] = out_7; R7[15:0] = out_8

  // Notes on the sheet:
  //   PC Circuit
  //   Register File
  //   contents of rom_1 (hex, n*v repeats v):
  //   9384 3b4d 4cd 6001 6042 6083 3aa4 b24 914 d93 70f0 88a 7700 6804 f804 4193 58de 7000 353 6001 614a
  //   618b 113 6804 1038
  //   ALU
  //   Registers' Contents
  //   Instruction Memory
  //   Control Unit
  //   Decoding Instructions
  //   Data Memory
endmodule
